// Logisim project Heza_1_Processor.circ as structural Verilog: 2 circuits, main circuit CPU
module CPU (
  input  carry_in,
  output a_larger,
  output equal,
  output b_larger,
  output zero,
  output carry_out,
  output [15:0] c
);

  wire adder_1_cout, and_1_out, and_2_out, and_3_out, and_4_out, and_5_out, and_6_out, and_7_out, and_8_out,
       and_10_out, and_11_out, and_13_out, and_14_out, and_16_out, and_17_out, and_18_out, and_20_out,
       and_21_out, and_22_out, and_24_out, and_25_out, and_26_out, and_27_out, and_28_out, and_29_out,
       and_30_out, and_31_out, and_32_out, and_33_out, and_34_out, and_35_out, and_36_out, and_37_out,
       and_38_out, and_39_out, and_40_out, and_41_out, and_42_out, and_43_out, and_44_out, and_45_out,
       and_46_out, and_47_out, and_48_out, and_49_out, and_50_out, and_51_out, and_52_out, and_53_out,
       and_54_out, and_55_out, and_56_out, and_57_out, and_58_out, clk_2_out, controlled_buffer_2_out,
       d_ff_1_q, decoder_1_out0, decoder_1_out1, decoder_1_out2, decoder_1_out3, decoder_1_out4,
       decoder_5_out0, decoder_5_out1, decoder_5_out2, decoder_5_out3, decoder_5_out4, decoder_5_out5,
       decoder_5_out6, decoder_5_out7, decoder_5_out8, decoder_5_out9, decoder_7_out0, decoder_7_out1,
       decoder_7_out2, decoder_7_out3, decoder_7_out4, decoder_7_out5, decoder_8_out0, decoder_8_out1,
       decoder_8_out2, decoder_8_out3, decoder_8_out4, decoder_8_out5, header_1_out_4, header_1_out_5,
       header_1_out_6, multiplexer_1_out, multiplexer_8_out, multiplexer_9_out, multiplexer_10_out,
       multiplexer_11_out, multiplexer_12_out, multiplexer_15_out, multiplexer_16_out, multiplexer_17_out,
       not_1_out, not_4_out, not_5_out, or_1_out, or_2_out, or_4_out, or_5_out, or_6_out, or_7_out, r_out,
       subtractor_1_bout, xnor_1_out;
  wire [1:0] multiplexer_14_out;
  wire [2:0] controlled_buffer_1_out, controlled_buffer_1_out_2, controlled_buffer_1_out_6, counter_1_q;
  wire [3:0] and_9_out, bit_extender_1_out, bit_extender_2_out, controlled_buffer_1_out_3,
       controlled_buffer_1_out_7, decoder_2_out0, multiplexer_4_out, multiplexer_5_out;
  wire [4:0] a_l_q, controlled_buffer_1_out_5;
  wire [15:0] adder_1_out, and_23_out, controlled_buffer_20_out, divider_1_out, IP_q, IR_q,
       multiplexer_6_out, multiplexer_7_out, multiplexer_13_out, multiplier_1_out, not_2_out, or_3_out,
       REG_00_q, REG_01_q, REG_02_q, REG_03_q, subtractor_1_out, xor_1_out;
  wire [15:8] multiplexer_14_out_2;
  wire [21:10] undriven_4, undriven_5, undriven_6;
  wire [25:6] decoder_9_out0;
  wire [25:10] controlled_buffer_1_out_4;
  wire [25:22] decoder_4_out0;
  wire [29:0] controlled_buffer_41_out, controlled_buffer_42_out, controlled_buffer_43_out,
       multiplexer_2_out, undriven, undriven_2, undriven_3;
  wire [29:26] decoder_6_out0;

  LED CLK (.in(xnor_1_out));
  LED END (.in(and_4_out));
  Button r (.out(r_out));
  Clock clk_2 (.out(clk_2_out));
  // Probe on REG_00_q
  D_Flip_Flop d_ff_1 (.clk(r_out), .D(clk_2_out), .Q(d_ff_1_q));  // open: Qn, preset, en, reset
  // Probe on REG_01_q
  // Probe on REG_02_q
  xnor xnor_1 (xnor_1_out, d_ff_1_q, clk_2_out);
  Counter #(.width(3), .max('h7)) counter_1 (
    .load(1'b0), .count(1'b1), .Q(counter_1_q), .clk(xnor_1_out), .clr(multiplexer_1_out));  // open: D, carry
  Multiplexer #(.disabled(0), .enable("false")) multiplexer_1 (
    .in0(or_1_out), .in1(r_out), .out(multiplexer_1_out), .sel(r_out));
  or or_1 (or_1_out, decoder_1_out4, controlled_buffer_2_out);
  // Probe on c
  // Probe on REG_03_q
  header header_1 (
    .out_4(header_1_out_4), .out_5(header_1_out_5), .out_6(header_1_out_6), .in_1(header_1_out_4),
    .in_2(header_1_out_5), .in_3(header_1_out_6));
  // Probe on controlled_buffer_20_out
  // Probe on controlled_buffer_20_out
  Decoder #(.select(3), .disabled(0), .enable("false")) decoder_1 (
    .out0(decoder_1_out0), .out1(decoder_1_out1), .out2(decoder_1_out2), .out3(decoder_1_out3),
    .out4(decoder_1_out4), .sel(counter_1_q));  // open: out5, out6, out7
  // Probe on IR_q
  // Probe on IP_q
  Multiplexer #(.width(30), .enable("false")) multiplexer_2 (
    .in0({undriven_2[29:22], 4'b1100, undriven_2[17], 1'b0, undriven_2[15:11], 1'b0, undriven_2[9:0]}),
    .in1(undriven_3), .out(multiplexer_2_out), .sel(r_out));
  assign {controlled_buffer_1_out_7, controlled_buffer_1_out_4[25:21], controlled_buffer_1_out_6, controlled_buffer_1_out_4[17:16], controlled_buffer_1_out_5, controlled_buffer_1_out_4[10], controlled_buffer_1_out_3, controlled_buffer_1_out_2, controlled_buffer_1_out} = decoder_1_out0 ? multiplexer_2_out : 30'bz;  // Controlled_Buffer controlled_buffer_1
  assign controlled_buffer_2_out = and_5_out ? 1'b1 : 1'bz;  // Controlled_Buffer controlled_buffer_2
  and and_1 (and_1_out, and_27_out, decoder_1_out0);
  assign {controlled_buffer_1_out_7, controlled_buffer_1_out_4[25:21], controlled_buffer_1_out_6, controlled_buffer_1_out_4[17:16], controlled_buffer_1_out_5, controlled_buffer_1_out_4[10], controlled_buffer_1_out_3, controlled_buffer_1_out_2, controlled_buffer_1_out} = and_5_out ? {undriven[29:18], 1'b1, undriven[16], {5{1'b0}}, undriven[10], 8'ha, undriven[1:0]} : 30'bz;  // Controlled_Buffer controlled_buffer_3
  not not_1 (not_1_out, and_16_out);
  and and_2 (and_2_out, and_28_out, decoder_1_out0);
  assign {controlled_buffer_1_out_7, controlled_buffer_1_out_4[25:21], controlled_buffer_1_out_6, controlled_buffer_1_out_4[17:16], controlled_buffer_1_out_5, controlled_buffer_1_out_4[10], controlled_buffer_1_out_3, controlled_buffer_1_out_2, controlled_buffer_1_out} = and_2_out ? {{8{1'b0}}, undriven_4[21:18], 1'b1, undriven_4[16], {5{1'b0}}, undriven_4[10], 10'h2d} : 30'bz;  // Controlled_Buffer controlled_buffer_4
  assign controlled_buffer_2_out = and_2_out ? 1'b0 : 1'bz;  // Controlled_Buffer controlled_buffer_5
  and and_3 (and_3_out, and_29_out, decoder_1_out0);
  assign {controlled_buffer_1_out_7, controlled_buffer_1_out_4[25:21], controlled_buffer_1_out_6, controlled_buffer_1_out_4[17:16], controlled_buffer_1_out_5, controlled_buffer_1_out_4[10], controlled_buffer_1_out_3, controlled_buffer_1_out_2, controlled_buffer_1_out} = and_3_out ? {{8{1'b0}}, undriven_5[21:18], 1'b1, undriven_5[16], {5{1'b0}}, undriven_5[10], 10'h2d} : 30'bz;  // Controlled_Buffer controlled_buffer_6
  assign controlled_buffer_2_out = and_3_out ? 1'b0 : 1'bz;  // Controlled_Buffer controlled_buffer_7
  assign controlled_buffer_2_out = and_4_out ? 1'b1 : 1'bz;  // Controlled_Buffer controlled_buffer_8
  and and_4 (and_4_out, and_30_out, decoder_1_out0);
  assign {controlled_buffer_1_out_7, controlled_buffer_1_out_4[25:21], controlled_buffer_1_out_6, controlled_buffer_1_out_4[17:16], controlled_buffer_1_out_5, controlled_buffer_1_out_4[10], controlled_buffer_1_out_3, controlled_buffer_1_out_2, controlled_buffer_1_out} = and_4_out ? 30'h30002d : 30'bz;  // Controlled_Buffer controlled_buffer_9
  LED led (.in(a_l_q[2]));
  LED z (.in(a_l_q[3]));
  LED led_2 (.in(a_l_q[0]));
  LED led_3 (.in(a_l_q[1]));
  Register #(.width(16)) REG_00 (
    .D(controlled_buffer_20_out), .en(controlled_buffer_1_out_4[22]), .Q(REG_00_q), .clk(xnor_1_out),
    .clr(multiplexer_5_out[0]));
  Register #(.width(16)) REG_01 (
    .D(controlled_buffer_20_out), .en(controlled_buffer_1_out_4[23]), .Q(REG_01_q), .clk(xnor_1_out),
    .clr(multiplexer_5_out[1]));
  Register #(.width(16)) REG_02 (
    .D(controlled_buffer_20_out), .en(controlled_buffer_1_out_4[24]), .Q(REG_02_q), .clk(xnor_1_out),
    .clr(multiplexer_5_out[2]));
  Register #(.width(16)) REG_03 (
    .D(controlled_buffer_20_out), .en(controlled_buffer_1_out_4[25]), .Q(REG_03_q), .clk(xnor_1_out),
    .clr(multiplexer_5_out[3]));
  assign bit_extender_1_out = {{3{r_out}}, r_out};  // Bit_Extender bit_extender_1
  Multiplexer #(.width(4), .enable("false")) multiplexer_3 (
    .in0(4'b0000), .in1(multiplexer_4_out), .out(undriven[29:26]), .sel(multiplexer_14_out_2[8]));
  and and_5 (and_5_out, and_1_out, not_1_out);
  Multiplexer #(.width(4), .disabled(0), .enable("false")) multiplexer_4 (
    .in0(bit_extender_2_out), .in1(decoder_2_out0), .out(multiplexer_4_out), .sel(and_6_out));
  LED u_c (.in(a_l_q[4]));
  Multiplexer #(.width(4), .enable("false")) multiplexer_5 (
    .in0(controlled_buffer_1_out_7), .in1(bit_extender_1_out), .out(multiplexer_5_out), .sel(r_out));
  and and_6 (and_6_out, xnor_1_out, and_27_out);
  // Probe on decoder_2_out0
  assign bit_extender_2_out = {{3{and_6_out}}, and_6_out};  // Bit_Extender bit_extender_2
  and and_7 (and_7_out, ~multiplexer_14_out[1], ~undriven[1]);  // AND_Gate
  // Probe on undriven[25:22]
  and and_8 (and_8_out, ~multiplexer_14_out[0], ~undriven[0]);  // AND_Gate
  and and_9 (and_9_out[0], and_7_out, and_8_out);
  and and_10 (and_10_out, multiplexer_14_out[0], undriven[0]);
  and and_11 (and_11_out, ~multiplexer_14_out[1], ~undriven[1]);  // AND_Gate
  and and_12 (and_9_out[1], and_11_out, and_10_out);
  or or_2 (or_2_out, and_9_out[0], and_9_out[1], and_9_out[2], and_9_out[3]);
  assign controlled_buffer_2_out = and_16_out ? 1'b0 : 1'bz;  // Controlled_Buffer controlled_buffer_10
  assign {controlled_buffer_1_out_7, controlled_buffer_1_out_4[25:21], controlled_buffer_1_out_6, controlled_buffer_1_out_4[17:16], controlled_buffer_1_out_5, controlled_buffer_1_out_4[10], controlled_buffer_1_out_3, controlled_buffer_1_out_2, controlled_buffer_1_out} = and_16_out ? {{8{1'b0}}, undriven_6[21:18], 1'b1, undriven_6[16], {5{1'b0}}, undriven_6[10], 10'h2d} : 30'bz;  // Controlled_Buffer controlled_buffer_11
  Decoder #(.select(2), .disabled(0), .enable("false")) decoder_2 (
    .out0(decoder_2_out0[0]), .out1(decoder_2_out0[1]), .out2(decoder_2_out0[2]), .out3(decoder_2_out0[3]),
    .sel(undriven[1:0]));
  and and_13 (and_13_out, multiplexer_14_out[1], undriven[1]);
  and and_14 (and_14_out, ~multiplexer_14_out[0], ~undriven[0]);  // AND_Gate
  and and_15 (and_9_out[2], and_13_out, and_14_out);
  and and_16 (and_16_out, or_2_out, and_1_out);
  Decoder #(.select(2), .disabled(0), .enable("false")) decoder_3 (
    .out0(undriven[22]), .out1(undriven[23]), .out2(undriven[24]), .out3(undriven[25]),
    .sel(multiplexer_14_out));
  and and_17 (and_17_out, multiplexer_14_out[1], undriven[1]);
  and and_18 (and_18_out, multiplexer_14_out[0], undriven[0]);
  and and_19 (and_9_out[3], and_17_out, and_18_out);
  Decoder #(.select(2), .disabled(0), .enable("false")) decoder_4 (
    .out0(decoder_4_out0[22]), .out1(decoder_4_out0[23]), .out2(decoder_4_out0[24]),
    .out3(decoder_4_out0[25]), .sel(multiplexer_14_out));
  Multiplexer #(.select(3), .width(16), .disabled(0), .enable("false")) multiplexer_6 (
    .in0(REG_00_q), .in1(REG_01_q), .in2(REG_02_q), .in3(REG_03_q), .in4(c), .in5({16{1'b0}}),
    .out(multiplexer_6_out), .sel(controlled_buffer_1_out));  // open: in6, in7
  Multiplexer #(.select(3), .width(16), .disabled(0), .enable("false")) multiplexer_7 (
    .in0(REG_00_q), .in1(REG_01_q), .in2(REG_02_q), .in3(REG_03_q), .in4(c), .in5({16{1'b0}}),
    .out(multiplexer_7_out), .sel(controlled_buffer_1_out_2));  // open: in6, in7
  // Probe on multiplexer_6_out
  // Probe on multiplexer_7_out
  and and_20 (and_20_out, and_27_out, decoder_1_out1);
  and and_21 (and_21_out, and_28_out, decoder_1_out1);
  and and_22 (and_22_out, and_29_out, decoder_1_out1);
  assign controlled_buffer_2_out = and_20_out ? 1'b0 : 1'bz;  // Controlled_Buffer controlled_buffer_12
  assign {controlled_buffer_1_out_7, controlled_buffer_1_out_4[25:21], controlled_buffer_1_out_6, controlled_buffer_1_out_4[17:16], controlled_buffer_1_out_5, controlled_buffer_1_out_4[10], controlled_buffer_1_out_3, controlled_buffer_1_out_2, controlled_buffer_1_out} = and_20_out ? {4'b0000, and_9_out, 22'h320025} : 30'bz;  // Controlled_Buffer controlled_buffer_13
  assign {controlled_buffer_1_out_7, controlled_buffer_1_out_4[25:21], controlled_buffer_1_out_6, controlled_buffer_1_out_4[17:16], controlled_buffer_1_out_5, controlled_buffer_1_out_4[10], controlled_buffer_1_out_3, controlled_buffer_1_out_2, controlled_buffer_1_out} = and_21_out ? {{10{1'b0}}, multiplexer_14_out, 13'h20, undriven[1:0], 3'b101} : 30'bz;  // Controlled_Buffer controlled_buffer_14
  assign controlled_buffer_2_out = and_21_out ? 1'b0 : 1'bz;  // Controlled_Buffer controlled_buffer_15
  assign {controlled_buffer_1_out_7, controlled_buffer_1_out_4[25:21], controlled_buffer_1_out_6, controlled_buffer_1_out_4[17:16], controlled_buffer_1_out_5, controlled_buffer_1_out_4[10], controlled_buffer_1_out_3, controlled_buffer_1_out_2, controlled_buffer_1_out} = and_22_out ? {4'b0000, decoder_4_out0, 2'b10, undriven[1:0], 18'h25} : 30'bz;  // Controlled_Buffer controlled_buffer_16
  assign controlled_buffer_2_out = and_22_out ? 1'b0 : 1'bz;  // Controlled_Buffer controlled_buffer_17
  Adder #(.width(16)) adder_1 (
    .a(multiplexer_6_out), .b(multiplexer_7_out), .out(adder_1_out), .cin(multiplexer_9_out),
    .cout(adder_1_cout));
  Subtractor #(.width(16)) subtractor_1 (
    .a(multiplexer_6_out), .b(multiplexer_7_out), .out(subtractor_1_out), .bin(multiplexer_8_out),
    .bout(subtractor_1_bout));
  Multiplier #(.width(16)) multiplier_1 (
    .a(multiplexer_6_out), .b(multiplexer_7_out), .out(multiplier_1_out), .cin({16{1'b0}}));  // open: cout
  Divider #(.width(16)) divider_1 (
    .a(multiplexer_6_out), .b(multiplexer_7_out), .out(divider_1_out));  // open: upper, rem
  assign not_2_out = ~multiplexer_6_out;  // NOT_Gate not_2, 16 bits wide
  assign and_23_out = multiplexer_6_out & multiplexer_7_out;  // AND_Gate and_23, 16 bits wide
  assign or_3_out = multiplexer_6_out | multiplexer_7_out;  // OR_Gate or_3, 16 bits wide
  assign xor_1_out = multiplexer_6_out ^ multiplexer_7_out;  // XOR_Gate xor_1, 16 bits wide
  Decoder #(.select(4), .enable("false")) decoder_5 (
    .out0(decoder_5_out0), .out1(decoder_5_out1), .out2(decoder_5_out2), .out3(decoder_5_out3),
    .out4(decoder_5_out4), .out5(decoder_5_out5), .out6(decoder_5_out6), .out7(decoder_5_out7),
    .out8(decoder_5_out8), .out9(decoder_5_out9), .sel(controlled_buffer_1_out_3));  // open: out10, out11, out12, out13, out14, out15
  Comparator #(.width(16)) comparator_1 (
    .a(multiplexer_6_out), .b(multiplexer_7_out), .gt(a_larger), .eq(equal), .lt(b_larger));
  assign carry_out = decoder_5_out2 ? 1'b0 : 1'bz;  // Controlled_Buffer controlled_buffer_18
  assign carry_out = decoder_5_out3 ? 1'b0 : 1'bz;  // Controlled_Buffer controlled_buffer_19
  assign controlled_buffer_20_out = decoder_5_out0 ? adder_1_out : 16'bz;  // Controlled_Buffer controlled_buffer_20
  assign carry_out = decoder_5_out0 ? adder_1_cout : 1'bz;  // Controlled_Buffer controlled_buffer_21
  assign controlled_buffer_20_out = decoder_5_out1 ? subtractor_1_out : 16'bz;  // Controlled_Buffer controlled_buffer_22
  assign carry_out = decoder_5_out1 ? subtractor_1_bout : 1'bz;  // Controlled_Buffer controlled_buffer_23
  assign controlled_buffer_20_out = decoder_5_out2 ? multiplier_1_out : 16'bz;  // Controlled_Buffer controlled_buffer_24
  assign controlled_buffer_20_out = decoder_5_out3 ? divider_1_out : 16'bz;  // Controlled_Buffer controlled_buffer_25
  assign controlled_buffer_20_out = decoder_5_out6 ? not_2_out : 16'bz;  // Controlled_Buffer controlled_buffer_26
  assign controlled_buffer_20_out = decoder_5_out7 ? and_23_out : 16'bz;  // Controlled_Buffer controlled_buffer_27
  assign controlled_buffer_20_out = decoder_5_out8 ? or_3_out : 16'bz;  // Controlled_Buffer controlled_buffer_28
  assign controlled_buffer_20_out = decoder_5_out9 ? xor_1_out : 16'bz;  // Controlled_Buffer controlled_buffer_29
  assign controlled_buffer_20_out = decoder_5_out4 ? {multiplexer_6_out[14:0], 1'b0} : 16'bz;  // Controlled_Buffer controlled_buffer_30
  assign carry_out = decoder_5_out4 ? multiplexer_6_out[15] : 1'bz;  // Controlled_Buffer controlled_buffer_31
  assign controlled_buffer_20_out = decoder_5_out5 ? {1'b0, multiplexer_6_out[15:1]} : 16'bz;  // Controlled_Buffer controlled_buffer_32
  assign carry_out = decoder_5_out5 ? multiplexer_6_out[0] : 1'bz;  // Controlled_Buffer controlled_buffer_33
  Multiplexer #(.enable("false")) multiplexer_8 (
    .in0(1'b0), .in1(carry_in), .out(multiplexer_8_out), .sel(decoder_5_out1));
  or or_4 (or_4_out, decoder_5_out6, decoder_5_out7, decoder_5_out8, decoder_5_out9);
  and and_24 (and_24_out, and_27_out, decoder_1_out2);
  assign controlled_buffer_2_out = and_24_out ? multiplexer_10_out : 1'bz;  // Controlled_Buffer controlled_buffer_34
  assign {controlled_buffer_1_out_7, controlled_buffer_1_out_4[25:21], controlled_buffer_1_out_6, controlled_buffer_1_out_4[17:16], controlled_buffer_1_out_5, controlled_buffer_1_out_4[10], controlled_buffer_1_out_3, controlled_buffer_1_out_2, controlled_buffer_1_out} = and_24_out ? controlled_buffer_41_out : 30'bz;  // Controlled_Buffer controlled_buffer_35
  and and_25 (and_25_out, and_28_out, decoder_1_out2);
  assign controlled_buffer_2_out = and_25_out ? multiplexer_11_out : 1'bz;  // Controlled_Buffer controlled_buffer_36
  assign {controlled_buffer_1_out_7, controlled_buffer_1_out_4[25:21], controlled_buffer_1_out_6, controlled_buffer_1_out_4[17:16], controlled_buffer_1_out_5, controlled_buffer_1_out_4[10], controlled_buffer_1_out_3, controlled_buffer_1_out_2, controlled_buffer_1_out} = and_25_out ? controlled_buffer_42_out : 30'bz;  // Controlled_Buffer controlled_buffer_37
  and and_26 (and_26_out, and_29_out, decoder_1_out2);
  assign controlled_buffer_2_out = and_26_out ? multiplexer_12_out : 1'bz;  // Controlled_Buffer controlled_buffer_38
  assign {controlled_buffer_1_out_7, controlled_buffer_1_out_4[25:21], controlled_buffer_1_out_6, controlled_buffer_1_out_4[17:16], controlled_buffer_1_out_5, controlled_buffer_1_out_4[10], controlled_buffer_1_out_3, controlled_buffer_1_out_2, controlled_buffer_1_out} = and_26_out ? controlled_buffer_43_out : 30'bz;  // Controlled_Buffer controlled_buffer_39
  Multiplexer #(.enable("false")) multiplexer_9 (
    .in0(1'b0), .in1(carry_in), .out(multiplexer_9_out), .sel(decoder_5_out0));
  assign carry_out = or_4_out ? 1'b0 : 1'bz;  // Controlled_Buffer controlled_buffer_40
  Multiplexer #(.enable("false")) multiplexer_10 (.in0(1'b0), .in1(1'b1), .out(multiplexer_10_out), .sel(and_24_out));
  assign controlled_buffer_41_out = and_24_out ? 30'h32002d : 30'bz;  // Controlled_Buffer controlled_buffer_41
  Multiplexer #(.enable("false")) multiplexer_11 (.in0(1'b0), .in1(1'b1), .out(multiplexer_11_out), .sel(and_25_out));
  assign controlled_buffer_42_out = and_25_out ? 30'h32002d : 30'bz;  // Controlled_Buffer controlled_buffer_42
  Multiplexer #(.enable("false")) multiplexer_12 (.in0(1'b0), .in1(1'b1), .out(multiplexer_12_out), .sel(and_26_out));
  assign controlled_buffer_43_out = and_26_out ? 30'h32002d : 30'bz;  // Controlled_Buffer controlled_buffer_43
  or or_5 (or_5_out, controlled_buffer_20_out[0], controlled_buffer_20_out[1], controlled_buffer_20_out[2], controlled_buffer_20_out[3], controlled_buffer_20_out[4], controlled_buffer_20_out[5], controlled_buffer_20_out[6], controlled_buffer_20_out[7], controlled_buffer_20_out[8], controlled_buffer_20_out[9], controlled_buffer_20_out[10], controlled_buffer_20_out[11], controlled_buffer_20_out[12], controlled_buffer_20_out[13], controlled_buffer_20_out[14], controlled_buffer_20_out[15]);
  not not_3 (zero, or_5_out);
  Counter #(.width(16), .max('hffff), .ongoal("continue")) IP (
    .load(controlled_buffer_1_out_4[16]), .D(controlled_buffer_20_out),
    .count(controlled_buffer_1_out_4[17]), .Q(IP_q), .clk(xnor_1_out), .clr(r_out));  // open: carry
  Register #(.width(1)) a_l (
    .D(a_larger), .en(controlled_buffer_1_out_5[0]), .Q(a_l_q[0]), .clk(xnor_1_out), .clr(r_out));
  Multiplexer #(.select(3), .width(16), .disabled(0), .enable("false")) multiplexer_13 (
    .in0(REG_00_q), .in1(REG_01_q), .in2(REG_02_q), .in3(REG_03_q), .in4(IP_q), .in5(multiplexer_6_out),
    .in6(multiplexer_7_out), .in7({16{1'b0}}), .out(multiplexer_13_out), .sel(controlled_buffer_1_out_6));
  Register #(.width(1)) equ (.D(equal), .en(controlled_buffer_1_out_5[1]), .Q(a_l_q[1]), .clk(xnor_1_out), .clr(r_out));
  Register #(.width(1)) b_l (
    .D(b_larger), .en(controlled_buffer_1_out_5[2]), .Q(a_l_q[2]), .clk(xnor_1_out), .clr(r_out));
  assign c = controlled_buffer_1_out_4[10] ? controlled_buffer_20_out : 16'bz;  // Controlled_Buffer controlled_buffer_44
  RAM #(.addrWidth(16), .dataWidth(16)) ram_1 (
    .addr(multiplexer_13_out), .data(c), .sel(1'b1), .clk(xnor_1_out), .ld(controlled_buffer_1_out_4[21]),
    .clr(1'b0));
  Register #(.width(1)) u_zero (
    .D(zero), .en(controlled_buffer_1_out_5[3]), .Q(a_l_q[3]), .clk(xnor_1_out), .clr(r_out));
  Register #(.width(1)) c_out (
    .D(carry_out), .en(controlled_buffer_1_out_5[4]), .Q(a_l_q[4]), .clk(xnor_1_out), .clr(r_out));
  Register #(.width(16), .trigger("falling")) IR (.D(c), .en(decoder_1_out0), .Q(IR_q), .clk(xnor_1_out), .clr(r_out));
  Multiplexer #(.width(16), .enable("false")) multiplexer_14 (
    .in0(IR_q), .in1(16'haaaa),
    .out({multiplexer_14_out_2, decoder_9_out0[9:6], undriven[1:0], multiplexer_14_out}), .sel(r_out));
  // Probe on {multiplexer_14_out_2, decoder_9_out0[9:6], undriven[1:0], multiplexer_14_out}
  and and_27 (and_27_out, ~multiplexer_14_out_2[9], ~multiplexer_14_out_2[10], ~multiplexer_14_out_2[11], ~multiplexer_14_out_2[12], ~multiplexer_14_out_2[13], ~multiplexer_14_out_2[14], ~multiplexer_14_out_2[15]);  // AND_Gate
  and and_28 (and_28_out, multiplexer_14_out_2[8], multiplexer_14_out_2[9], ~multiplexer_14_out_2[10], ~multiplexer_14_out_2[11], ~multiplexer_14_out_2[12], ~multiplexer_14_out_2[13], ~multiplexer_14_out_2[14], ~multiplexer_14_out_2[15]);  // AND_Gate
  and and_29 (and_29_out, ~multiplexer_14_out_2[8], multiplexer_14_out_2[9], ~multiplexer_14_out_2[10], ~multiplexer_14_out_2[11], ~multiplexer_14_out_2[12], ~multiplexer_14_out_2[13], ~multiplexer_14_out_2[14], ~multiplexer_14_out_2[15]);  // AND_Gate
  and and_30 (and_30_out, ~multiplexer_14_out[0], multiplexer_14_out[1], ~undriven[0], undriven[1], ~decoder_9_out0[6], decoder_9_out0[7], ~decoder_9_out0[8], decoder_9_out0[9], ~multiplexer_14_out_2[8], multiplexer_14_out_2[9], ~multiplexer_14_out_2[10], multiplexer_14_out_2[11], ~multiplexer_14_out_2[12], multiplexer_14_out_2[13], ~multiplexer_14_out_2[14], multiplexer_14_out_2[15]);  // AND_Gate
  and and_31 (and_31_out, and_57_out, decoder_1_out0);
  assign {controlled_buffer_1_out_7, controlled_buffer_1_out_4[25:21], controlled_buffer_1_out_6, controlled_buffer_1_out_4[17:16], controlled_buffer_1_out_5, controlled_buffer_1_out_4[10], controlled_buffer_1_out_3, controlled_buffer_1_out_2, controlled_buffer_1_out} = and_31_out ? 30'h30002d : 30'bz;  // Controlled_Buffer controlled_buffer_45
  assign controlled_buffer_2_out = and_31_out ? 1'b0 : 1'bz;  // Controlled_Buffer controlled_buffer_46
  and and_32 (and_32_out, and_58_out, decoder_1_out0);
  assign {controlled_buffer_1_out_7, controlled_buffer_1_out_4[25:21], controlled_buffer_1_out_6, controlled_buffer_1_out_4[17:16], controlled_buffer_1_out_5, controlled_buffer_1_out_4[10], controlled_buffer_1_out_3, controlled_buffer_1_out_2, controlled_buffer_1_out} = and_32_out ? 30'h32002d : 30'bz;  // Controlled_Buffer controlled_buffer_47
  assign controlled_buffer_2_out = and_32_out ? 1'b0 : 1'bz;  // Controlled_Buffer controlled_buffer_48
  and and_33 (and_33_out, and_55_out, decoder_1_out0);
  and and_34 (and_34_out, and_56_out, decoder_1_out0);
  assign {controlled_buffer_1_out_7, controlled_buffer_1_out_4[25:21], controlled_buffer_1_out_6, controlled_buffer_1_out_4[17:16], controlled_buffer_1_out_5, controlled_buffer_1_out_4[10], controlled_buffer_1_out_3, controlled_buffer_1_out_2, controlled_buffer_1_out} = and_33_out ? 30'h30002d : 30'bz;  // Controlled_Buffer controlled_buffer_49
  assign controlled_buffer_2_out = and_33_out ? 1'b0 : 1'bz;  // Controlled_Buffer controlled_buffer_50
  assign {controlled_buffer_1_out_7, controlled_buffer_1_out_4[25:21], controlled_buffer_1_out_6, controlled_buffer_1_out_4[17:16], controlled_buffer_1_out_5, controlled_buffer_1_out_4[10], controlled_buffer_1_out_3, controlled_buffer_1_out_2, controlled_buffer_1_out} = and_34_out ? {decoder_6_out0, 26'h32002d} : 30'bz;  // Controlled_Buffer controlled_buffer_51
  assign controlled_buffer_2_out = and_34_out ? 1'b1 : 1'bz;  // Controlled_Buffer controlled_buffer_52
  Decoder #(.select(2), .enable("false")) decoder_6 (
    .out0(decoder_6_out0[26]), .out1(decoder_6_out0[27]), .out2(decoder_6_out0[28]),
    .out3(decoder_6_out0[29]), .sel(multiplexer_14_out));
  and and_35 (and_35_out, and_57_out, decoder_1_out1);
  and and_36 (and_36_out, and_35_out, not_4_out);
  assign {controlled_buffer_1_out_7, controlled_buffer_1_out_4[25:21], controlled_buffer_1_out_6, controlled_buffer_1_out_4[17:16], controlled_buffer_1_out_5, controlled_buffer_1_out_4[10], controlled_buffer_1_out_3, controlled_buffer_1_out_2, controlled_buffer_1_out} = and_36_out ? 30'h32002d : 30'bz;  // Controlled_Buffer controlled_buffer_53
  assign controlled_buffer_2_out = and_36_out ? 1'b0 : 1'bz;  // Controlled_Buffer controlled_buffer_54
  assign {controlled_buffer_1_out_7, controlled_buffer_1_out_4[25:21], controlled_buffer_1_out_6, controlled_buffer_1_out_4[17:16], controlled_buffer_1_out_5, controlled_buffer_1_out_4[10], controlled_buffer_1_out_3, controlled_buffer_1_out_2, controlled_buffer_1_out} = and_40_out ? {28'hc400a, multiplexer_14_out} : 30'bz;  // Controlled_Buffer controlled_buffer_55
  assign controlled_buffer_2_out = and_40_out ? 1'b0 : 1'bz;  // Controlled_Buffer controlled_buffer_56
  and and_37 (and_37_out, and_58_out, decoder_1_out1);
  and and_38 (and_38_out, and_37_out, not_5_out);
  assign {controlled_buffer_1_out_7, controlled_buffer_1_out_4[25:21], controlled_buffer_1_out_6, controlled_buffer_1_out_4[17:16], controlled_buffer_1_out_5, controlled_buffer_1_out_4[10], controlled_buffer_1_out_3, controlled_buffer_1_out_2, controlled_buffer_1_out} = and_38_out ? 30'h32002d : 30'bz;  // Controlled_Buffer controlled_buffer_57
  assign controlled_buffer_2_out = and_38_out ? 1'b0 : 1'bz;  // Controlled_Buffer controlled_buffer_58
  assign {controlled_buffer_1_out_7, controlled_buffer_1_out_4[25:21], controlled_buffer_1_out_6, controlled_buffer_1_out_4[17:16], controlled_buffer_1_out_5, controlled_buffer_1_out_4[10], controlled_buffer_1_out_3, controlled_buffer_1_out_2, controlled_buffer_1_out} = and_41_out ? 30'h31002c : 30'bz;  // Controlled_Buffer controlled_buffer_59
  assign controlled_buffer_2_out = and_41_out ? 1'b0 : 1'bz;  // Controlled_Buffer controlled_buffer_60
  and and_39 (and_39_out, and_55_out, decoder_1_out1);
  and and_40 (and_40_out, and_35_out, or_6_out);
  and and_41 (and_41_out, and_37_out, or_7_out);
  not not_4 (not_4_out, or_6_out);
  not not_5 (not_5_out, or_7_out);
  assign controlled_buffer_2_out = and_39_out ? 1'b0 : 1'bz;  // Controlled_Buffer controlled_buffer_61
  assign {controlled_buffer_1_out_7, controlled_buffer_1_out_4[25:21], controlled_buffer_1_out_6, controlled_buffer_1_out_4[17:16], controlled_buffer_1_out_5, controlled_buffer_1_out_4[10], controlled_buffer_1_out_3, controlled_buffer_1_out_2, controlled_buffer_1_out} = and_39_out ? {4'b0000, decoder_9_out0[25:22], 12'hcbe, decoder_9_out0[9:6], 1'b0, multiplexer_14_out, 1'b0, undriven[1:0]} : 30'bz;  // Controlled_Buffer controlled_buffer_62
  and and_42 (and_42_out, a_l_q[0], decoder_7_out1);
  and and_43 (and_43_out, a_l_q[1], decoder_7_out0);
  and and_44 (and_44_out, a_l_q[1], decoder_8_out0);
  and and_45 (and_45_out, a_l_q[0], decoder_8_out1);
  Decoder #(.select(3), .enable("false")) decoder_7 (
    .out0(decoder_7_out0), .out1(decoder_7_out1), .out2(decoder_7_out2), .out3(decoder_7_out3),
    .out4(decoder_7_out4), .out5(decoder_7_out5), .sel(decoder_9_out0[8:6]));  // open: out6, out7
  and and_46 (and_46_out, a_l_q[2], decoder_7_out2);
  and and_47 (and_47_out, a_l_q[3], decoder_7_out3);
  or or_6 (or_6_out, and_43_out, and_42_out, and_46_out, and_47_out, and_50_out, decoder_7_out5);
  Decoder #(.select(3), .enable("false")) decoder_8 (
    .out0(decoder_8_out0), .out1(decoder_8_out1), .out2(decoder_8_out2), .out3(decoder_8_out3),
    .out4(decoder_8_out4), .out5(decoder_8_out5), .sel(decoder_9_out0[8:6]));  // open: out6, out7
  and and_48 (and_48_out, a_l_q[3], decoder_8_out3);
  and and_49 (and_49_out, a_l_q[2], decoder_8_out2);
  or or_7 (or_7_out, and_44_out, and_45_out, and_49_out, and_48_out, and_51_out, decoder_8_out5);
  and and_50 (and_50_out, a_l_q[4], decoder_7_out4);
  and and_51 (and_51_out, a_l_q[4], decoder_8_out4);
  Decoder #(.select(2), .disabled(0), .enable("false")) decoder_9 (
    .out0(decoder_9_out0[22]), .out1(decoder_9_out0[23]), .out2(decoder_9_out0[24]),
    .out3(decoder_9_out0[25]), .sel(undriven[1:0]));
  and and_52 (and_52_out, and_57_out, decoder_1_out2);
  assign controlled_buffer_2_out = and_52_out ? multiplexer_15_out : 1'bz;  // Controlled_Buffer controlled_buffer_63
  and and_53 (and_53_out, and_58_out, decoder_1_out2);
  assign controlled_buffer_2_out = and_53_out ? multiplexer_16_out : 1'bz;  // Controlled_Buffer controlled_buffer_64
  and and_54 (and_54_out, and_55_out, decoder_1_out2);
  assign controlled_buffer_2_out = and_54_out ? multiplexer_17_out : 1'bz;  // Controlled_Buffer controlled_buffer_65
  assign {controlled_buffer_1_out_7, controlled_buffer_1_out_4[25:21], controlled_buffer_1_out_6, controlled_buffer_1_out_4[17:16], controlled_buffer_1_out_5, controlled_buffer_1_out_4[10], controlled_buffer_1_out_3, controlled_buffer_1_out_2, controlled_buffer_1_out} = and_52_out ? 30'h32002d : 30'bz;  // Controlled_Buffer controlled_buffer_66
  assign {controlled_buffer_1_out_7, controlled_buffer_1_out_4[25:21], controlled_buffer_1_out_6, controlled_buffer_1_out_4[17:16], controlled_buffer_1_out_5, controlled_buffer_1_out_4[10], controlled_buffer_1_out_3, controlled_buffer_1_out_2, controlled_buffer_1_out} = and_53_out ? 30'h32002d : 30'bz;  // Controlled_Buffer controlled_buffer_67
  assign {controlled_buffer_1_out_7, controlled_buffer_1_out_4[25:21], controlled_buffer_1_out_6, controlled_buffer_1_out_4[17:16], controlled_buffer_1_out_5, controlled_buffer_1_out_4[10], controlled_buffer_1_out_3, controlled_buffer_1_out_2, controlled_buffer_1_out} = and_54_out ? 30'h32002d : 30'bz;  // Controlled_Buffer controlled_buffer_68
  Multiplexer #(.enable("false")) multiplexer_15 (.in0(1'b0), .in1(1'b1), .out(multiplexer_15_out), .sel(and_52_out));
  Multiplexer #(.enable("false")) multiplexer_16 (.in0(1'b0), .in1(1'b1), .out(multiplexer_16_out), .sel(and_53_out));
  Multiplexer #(.enable("false")) multiplexer_17 (.in0(1'b0), .in1(1'b1), .out(multiplexer_17_out), .sel(and_54_out));
  and and_55 (and_55_out, ~multiplexer_14_out_2[8], ~multiplexer_14_out_2[9], multiplexer_14_out_2[10], ~multiplexer_14_out_2[11], ~multiplexer_14_out_2[12], ~multiplexer_14_out_2[13], ~multiplexer_14_out_2[14], ~multiplexer_14_out_2[15]);  // AND_Gate
  and and_56 (and_56_out, multiplexer_14_out_2[8], multiplexer_14_out_2[9], multiplexer_14_out_2[10], ~multiplexer_14_out_2[11], ~multiplexer_14_out_2[12], ~multiplexer_14_out_2[13], ~multiplexer_14_out_2[14], ~multiplexer_14_out_2[15]);  // AND_Gate
  and and_57 (and_57_out, ~decoder_9_out0[9], multiplexer_14_out_2[8], ~multiplexer_14_out_2[9], multiplexer_14_out_2[10], ~multiplexer_14_out_2[11], ~multiplexer_14_out_2[12], ~multiplexer_14_out_2[13], ~multiplexer_14_out_2[14], ~multiplexer_14_out_2[15]);  // AND_Gate
  and and_58 (and_58_out, decoder_9_out0[9], multiplexer_14_out_2[8], ~multiplexer_14_out_2[9], multiplexer_14_out_2[10], ~multiplexer_14_out_2[11], ~multiplexer_14_out_2[12], ~multiplexer_14_out_2[13], ~multiplexer_14_out_2[14], ~multiplexer_14_out_2[15]);  // AND_Gate

  // Notes on the sheet:
  //   carry_in: pull=down
  //   c: pull=down
  //   reset
  //   (unstable) OVERWRITE RA, RB
  //   Ctrl + K
  //   Press
  //   Ctrl + R
  //   Press
  //   R0
  //   R1
  //   MOVE RA, RB
  //   MOVE IMM, R
  //   MOVE R, [R]
  //   MOVE [R], R
  //   END
  //   To get more information about the processor itself, please refer to the
  //   to start the clock
  //   to reset the simulation
  //   R2
  //   Program Counter
  //   To learn more about the instructions, see the 
  //   You can choose your clock speed from the top menu
  //   Select the Poke Tool (              ) from the topbar to start toggling buttons
  //   R3
  //   D_Bus
  //   Welcome to Heza 1 CPU
  //   Hi, and welcome to the Heza 1 Processor circuit diagram.
  //   To get more information, see the GitHub Repo.
  //   Enjoy (and don't fuck up the circuit lol)!
  //   ALU_Bus
  //   Instruction Table.
  //   "Simulate" > "Tick Frequency" > ...
  //   👆
  //   IR
  //   Heza 1 Processor User Manual.
  //   IP
  //   Flags
  //   a
  //   b
  //   RAM
  //   ALU OPERATIONS
  //   CLEAR REGISTERS
  //   UN/CONDITIONAL JUMP TO VALUE IN REGISTER
  //   UN/CONDITIONAL JUMP TO IMMEDIATE
endmodule

module header (
  input  in_1,
  input  in_2,
  input  in_3,
  output out_4,
  output out_5,
  output out_6
);

  not not_1 (out_4, 1'b1);
  not not_2 (out_6, 1'b0);
endmodule
