// Logisim project heza-cpu.circ as structural Verilog: 4 circuits, main circuit TOP
module TOP (
);

  wire circ_1_end__o, circ_1_flag_____o, circ_1_flag_____o_2, circ_1_flag_____o_3, circ_1_flag__c__o,
       circ_1_flag__z__o, circ_1_ram_ld__o, CLK_out, Reset_out;
  wire [15:0] circ_1_alu_bus__o, circ_1_d_bus__o, circ_1_ip__o, circ_1_ir__o, circ_1_r0__o, circ_1_r1__o,
       circ_1_r2__o, circ_1_r3__o, circ_1_ram_input__o, ram_1_ram_output__o;

  Clock CLK (.out(CLK_out));
  LED END (.in(circ_1_end__o));
  CIRC circ_1 (
    .RAM_LD__o(circ_1_ram_ld__o), .FLAG_____o(circ_1_flag_____o), .FLAG_____o_2(circ_1_flag_____o_2),
    .FLAG_____o_3(circ_1_flag_____o_3), .FLAG__z__o(circ_1_flag__z__o), .FLAG__c__o(circ_1_flag__c__o),
    .RAM_INPUT__o(circ_1_ram_input__o), .END__o(circ_1_end__o), .R0__o(circ_1_r0__o), .R1__o(circ_1_r1__o),
    .R2__o(circ_1_r2__o), .R3__o(circ_1_r3__o), .D_Bus__o(circ_1_d_bus__o), .ALU_Bus__o(circ_1_alu_bus__o),
    .IP__o(circ_1_ip__o), .IR__o(circ_1_ir__o), .CLK__i(CLK_out), .RESET__i(Reset_out),
    .D_Bus__i(ram_1_ram_output__o));  // open: CARRY_IN__i
  Button Reset (.out(Reset_out));
  // Probe on circ_1_r0__o
  // Probe on circ_1_r1__o
  // Probe on circ_1_r2__o
  // Probe on circ_1_r3__o
  // Probe on circ_1_ip__o
  // Probe on circ_1_d_bus__o
  // Probe on circ_1_ir__o
  // Probe on circ_1_alu_bus__o
  RAM ram_1 (
    .RAM_OUTPUT__o(ram_1_ram_output__o), .RAM_LD__i(circ_1_ram_ld__o), .CLK__i(CLK_out),
    .RAM_INPUT__i(circ_1_ram_input__o));
  LED led (.in(circ_1_flag_____o));
  LED led_2 (.in(circ_1_flag_____o_2));
  LED led_3 (.in(circ_1_flag_____o_3));
  LED z (.in(circ_1_flag__z__o));
  LED c (.in(circ_1_flag__c__o));

  // Notes on the sheet:
  //   Press [CTRL + K] to start or stop the Clock
  //   Press [CTRL + R] to reset the simulation
  //   CPU
  //   Welcome to Heza 1 Processor
  //   Welcome to the Logisim Evolution version of the Heza 1 CPU.
  //   To learn more about it, see the User Manual.
  //   To start coding a program for the Heza 1 processor, please refer to the Instruction Table.
  //   NOTE: The simulation of the "TOP" circuit (this one) is a bit slower than the simulation of the "CPU" circuit, where the RAM is embedded into the CPU.
  //   If you want a faster simulation, please open the "CPU" circuit instead
  //   Select the Hand icon from the topbar to start toggling buttons
  //   You can choose your clock speed from the top menu ("Simulate" > "Tick Frequency" > ...)
  //   RAM
  //   Flags
  //   To load a program, right click on the "RAM" item below and choose "View RAM", then load the program as described in the User Manual
endmodule

module CPU (
  input  CARRY_IN,
  input  CLK__i
);

  wire adder_1_cout, and_1_out, and_2_out, and_3_out, and_4_out, and_5_out, and_6_out, and_7_out, and_8_out,
       and_9_out, and_10_out, and_11_out, and_13_out, and_14_out, and_16_out, and_17_out, and_18_out,
       and_20_out, and_21_out, and_22_out, and_24_out, and_26_out, and_27_out, and_28_out, and_29_out,
       and_30_out, and_31_out, and_32_out, and_33_out, and_34_out, and_35_out, and_36_out, and_37_out,
       and_38_out, and_39_out, and_40_out, and_41_out, and_42_out, and_43_out, and_44_out, and_45_out,
       and_46_out, and_47_out, and_48_out, and_49_out, and_50_out, and_51_out, and_52_out, and_53_out,
       and_54_out, and_55_out, and_56_out, and_57_out, and_58_out, CLK_out, comparator_1_eq, comparator_1_gt,
       comparator_1_lt, controlled_buffer_1_out, controlled_buffer_35_out, d_ff_1_q, decoder_1_out0,
       decoder_1_out1, decoder_1_out2, decoder_1_out3, decoder_1_out4, decoder_5_out0, decoder_5_out1,
       decoder_5_out2, decoder_5_out3, decoder_5_out4, decoder_5_out5, decoder_5_out6, decoder_5_out7,
       decoder_5_out8, decoder_5_out9, decoder_8_out0, decoder_8_out1, decoder_8_out2, decoder_8_out3,
       decoder_8_out4, decoder_8_out5, decoder_9_out0, decoder_9_out1, decoder_9_out2, decoder_9_out3,
       decoder_9_out4, decoder_9_out5, multiplexer_4_out, multiplexer_5_out, nor_1_out, not_1_out, not_2_out,
       not_4_out, not_5_out, or_1_out, or_2_out, or_5_out, or_6_out, or_7_out, or_8_out, or_9_out, Reset_out,
       subtractor_1_bout, xor_1_out;
  wire [1:0] multiplexer_7_out;
  wire [2:0] controlled_buffer_2_out, controlled_buffer_2_out_2, counter_1_q;
  wire [3:0] bit_extender_1_out, controlled_buffer_2_out_3, controlled_buffer_2_out_5,
       controlled_buffer_2_out_6, decoder_4_out0, or_4_out;
  wire [4:0] register_1_q;
  wire [15:0] adder_1_out, and_25_out, controlled_buffer_39_out, controlled_buffer_64_out, counter_2_q,
       divider_1_out, multiplexer_2_out, multiplexer_3_out, multiplexer_6_out, multiplier_1_out, not_3_out,
       or_3_out, R0_2_q, R1_2_q, R2_2_q, R3_2_q, register_6_q, subtractor_1_out, xor_2_out;
  wire [15:8] multiplexer_7_out_3;
  wire [21:10] controlled_buffer_2_out_4;
  wire [25:6] multiplexer_7_out_2;
  wire [25:22] and_12_out, decoder_6_out0;
  wire [29:0] decoder_3_out0;
  wire [29:26] decoder_2_out0;

  Clock CLK (.out(CLK_out));
  LED END (.in(and_9_out));
  // Probe on R0_2_q
  Button Reset (.out(Reset_out));
  // Probe on R1_2_q
  // Probe on R2_2_q
  // Probe on R3_2_q
  // Probe on controlled_buffer_64_out
  // Probe on controlled_buffer_39_out
  // Probe on counter_2_q
  // Probe on register_6_q
  LED led (.in(register_1_q[0]));
  LED led_2 (.in(register_1_q[1]));
  LED led_3 (.in(register_1_q[2]));
  LED z (.in(register_1_q[3]));
  LED c (.in(register_1_q[4]));
  Counter #(.max('h7), .width(3)) counter_1 (
    .load(1'b0), .count(1'b1), .Q(counter_1_q), .up(1'b1), .clk(not_1_out), .clr(or_1_out));  // open: D, carry
  or or_1 (or_1_out, Reset_out, decoder_1_out4, controlled_buffer_1_out);
  Decoder #(.enable("false"), .select(3)) decoder_1 (
    .out0(decoder_1_out0), .out1(decoder_1_out1), .out2(decoder_1_out2), .out3(decoder_1_out3),
    .out4(decoder_1_out4), .sel(counter_1_q));  // open: out5, out6, out7
  D_Flip_Flop d_ff_1 (.clk(Reset_out), .D(CLK_out), .Q(d_ff_1_q));  // open: Qn, preset, reset
  xor xor_1 (xor_1_out, d_ff_1_q, CLK_out);
  not not_1 (not_1_out, xor_1_out);
  Register #(.width(16)) R0_2 (
    .D(controlled_buffer_39_out), .en(controlled_buffer_2_out_5[0]), .clk(not_1_out), .Q(R0_2_q),
    .clr(or_4_out[0]));
  Register #(.width(16)) R1_2 (
    .D(controlled_buffer_39_out), .en(controlled_buffer_2_out_5[1]), .clk(not_1_out), .Q(R1_2_q),
    .clr(or_4_out[1]));
  Register #(.width(16)) R2_2 (
    .D(controlled_buffer_39_out), .en(controlled_buffer_2_out_5[2]), .clk(not_1_out), .Q(R2_2_q),
    .clr(or_4_out[2]));
  Register #(.width(16)) R3_2 (
    .D(controlled_buffer_39_out), .en(controlled_buffer_2_out_5[3]), .clk(not_1_out), .Q(R3_2_q),
    .clr(or_4_out[3]));
  and and_1 (and_1_out, and_51_out, decoder_1_out0);
  and and_2 (and_2_out, and_1_out, not_2_out);
  not not_2 (not_2_out, and_20_out);
  assign controlled_buffer_1_out = and_2_out ? 1'b1 : 1'bz;  // Controlled_Buffer controlled_buffer_1
  and and_3 (and_3_out, and_54_out, decoder_1_out0);
  assign {controlled_buffer_2_out_6, controlled_buffer_2_out_5, controlled_buffer_2_out_4, controlled_buffer_2_out_3, controlled_buffer_2_out_2, controlled_buffer_2_out} = and_3_out ? 30'h32002d : 30'bz;  // Controlled_Buffer controlled_buffer_2
  and and_4 (and_4_out, and_55_out, decoder_1_out0);
  assign {controlled_buffer_2_out_6, controlled_buffer_2_out_5, controlled_buffer_2_out_4, controlled_buffer_2_out_3, controlled_buffer_2_out_2, controlled_buffer_2_out} = and_4_out ? 30'h32002d : 30'bz;  // Controlled_Buffer controlled_buffer_3
  and and_5 (and_5_out, and_56_out, decoder_1_out0);
  assign {controlled_buffer_2_out_6, controlled_buffer_2_out_5, controlled_buffer_2_out_4, controlled_buffer_2_out_3, controlled_buffer_2_out_2, controlled_buffer_2_out} = and_5_out ? 30'h30002d : 30'bz;  // Controlled_Buffer controlled_buffer_4
  and and_6 (and_6_out, and_57_out, decoder_1_out0);
  assign {controlled_buffer_2_out_6, controlled_buffer_2_out_5, controlled_buffer_2_out_4, controlled_buffer_2_out_3, controlled_buffer_2_out_2, controlled_buffer_2_out} = and_6_out ? {decoder_2_out0, 26'h32002d} : 30'bz;  // Controlled_Buffer controlled_buffer_5
  and and_7 (and_7_out, and_52_out, decoder_1_out0);
  assign {controlled_buffer_2_out_6, controlled_buffer_2_out_5, controlled_buffer_2_out_4, controlled_buffer_2_out_3, controlled_buffer_2_out_2, controlled_buffer_2_out} = and_7_out ? 30'h30002d : 30'bz;  // Controlled_Buffer controlled_buffer_6
  and and_8 (and_8_out, and_53_out, decoder_1_out0);
  assign {controlled_buffer_2_out_6, controlled_buffer_2_out_5, controlled_buffer_2_out_4, controlled_buffer_2_out_3, controlled_buffer_2_out_2, controlled_buffer_2_out} = and_8_out ? 30'h32002d : 30'bz;  // Controlled_Buffer controlled_buffer_7
  and and_9 (and_9_out, and_58_out, decoder_1_out0);
  assign {controlled_buffer_2_out_6, controlled_buffer_2_out_5, controlled_buffer_2_out_4, controlled_buffer_2_out_3, controlled_buffer_2_out_2, controlled_buffer_2_out} = and_9_out ? 30'h30002d : 30'bz;  // Controlled_Buffer controlled_buffer_8
  assign controlled_buffer_1_out = and_9_out ? 1'b1 : 1'bz;  // Controlled_Buffer controlled_buffer_9
  assign {controlled_buffer_2_out_6, controlled_buffer_2_out_5, controlled_buffer_2_out_4, controlled_buffer_2_out_3, controlled_buffer_2_out_2, controlled_buffer_2_out} = and_2_out ? {decoder_3_out0[29:22], 20'hc800a, decoder_3_out0[1:0]} : 30'bz;  // Controlled_Buffer controlled_buffer_10
  assign controlled_buffer_1_out = and_3_out ? 1'b0 : 1'bz;  // Controlled_Buffer controlled_buffer_11
  assign controlled_buffer_1_out = and_4_out ? 1'b0 : 1'bz;  // Controlled_Buffer controlled_buffer_12
  assign controlled_buffer_1_out = and_5_out ? 1'b0 : 1'bz;  // Controlled_Buffer controlled_buffer_13
  assign controlled_buffer_1_out = and_6_out ? 1'b1 : 1'bz;  // Controlled_Buffer controlled_buffer_14
  assign controlled_buffer_1_out = and_7_out ? 1'b0 : 1'bz;  // Controlled_Buffer controlled_buffer_15
  assign controlled_buffer_1_out = and_8_out ? 1'b0 : 1'bz;  // Controlled_Buffer controlled_buffer_16
  Multiplexer #(.enable("false"), .width(4)) multiplexer_1 (
    .in0(4'b0000), .in1(decoder_4_out0), .out(decoder_3_out0[29:26]), .sel(and_10_out));
  Decoder #(.enable("false"), .select(2)) decoder_2 (
    .out0(decoder_2_out0[26]), .out1(decoder_2_out0[27]), .out2(decoder_2_out0[28]),
    .out3(decoder_2_out0[29]), .sel(multiplexer_7_out));
  and and_10 (and_10_out, and_1_out, multiplexer_7_out_3[8]);
  and and_11 (and_11_out, ~multiplexer_7_out[0], ~decoder_3_out0[0]);  // AND_Gate
  and and_12 (and_12_out[22], and_11_out, and_13_out);
  Decoder #(.enable("false"), .select(2)) decoder_3 (
    .out0(decoder_3_out0[22]), .out1(decoder_3_out0[23]), .out2(decoder_3_out0[24]),
    .out3(decoder_3_out0[25]), .sel(multiplexer_7_out));
  Decoder #(.enable("false"), .select(2)) decoder_4 (
    .out0(decoder_4_out0[0]), .out1(decoder_4_out0[1]), .out2(decoder_4_out0[2]), .out3(decoder_4_out0[3]),
    .sel(decoder_3_out0[1:0]));
  and and_13 (and_13_out, ~multiplexer_7_out[1], ~decoder_3_out0[1]);  // AND_Gate
  and and_14 (and_14_out, multiplexer_7_out[0], decoder_3_out0[0]);
  and and_15 (and_12_out[23], and_14_out, and_16_out);
  and and_16 (and_16_out, ~multiplexer_7_out[1], ~decoder_3_out0[1]);  // AND_Gate
  and and_17 (and_17_out, ~multiplexer_7_out[0], ~decoder_3_out0[0]);  // AND_Gate
  and and_18 (and_18_out, multiplexer_7_out[1], decoder_3_out0[1]);
  and and_19 (and_12_out[24], and_17_out, and_18_out);
  or or_2 (or_2_out, and_12_out[22], and_12_out[23], and_12_out[24], and_12_out[25]);
  and and_20 (and_20_out, and_1_out, or_2_out);
  assign {controlled_buffer_2_out_6, controlled_buffer_2_out_5, controlled_buffer_2_out_4, controlled_buffer_2_out_3, controlled_buffer_2_out_2, controlled_buffer_2_out} = and_20_out ? 30'h32002d : 30'bz;  // Controlled_Buffer controlled_buffer_17
  assign controlled_buffer_1_out = and_20_out ? 1'b0 : 1'bz;  // Controlled_Buffer controlled_buffer_18
  and and_21 (and_21_out, multiplexer_7_out[0], decoder_3_out0[0]);
  and and_22 (and_22_out, multiplexer_7_out[1], decoder_3_out0[1]);
  and and_23 (and_12_out[25], and_21_out, and_22_out);
  Multiplexer #(.enable("false"), .select(3), .width(16)) multiplexer_2 (
    .in0(R0_2_q), .in1(R1_2_q), .in2(R2_2_q), .in3(R3_2_q), .in4(controlled_buffer_64_out), .in5({16{1'b0}}),
    .out(multiplexer_2_out), .sel(controlled_buffer_2_out));  // open: in6, in7
  Multiplexer #(.enable("false"), .select(3), .width(16)) multiplexer_3 (
    .in0(R0_2_q), .in1(R1_2_q), .in2(R2_2_q), .in3(R3_2_q), .in4(controlled_buffer_64_out), .in5({16{1'b0}}),
    .out(multiplexer_3_out), .sel(controlled_buffer_2_out_2));  // open: in6, in7
  and and_24 (and_24_out, and_51_out, decoder_1_out1);
  assign {controlled_buffer_2_out_6, controlled_buffer_2_out_5, controlled_buffer_2_out_4, controlled_buffer_2_out_3, controlled_buffer_2_out_2, controlled_buffer_2_out} = and_24_out ? {4'b0000, and_12_out, 22'h320025} : 30'bz;  // Controlled_Buffer controlled_buffer_19
  assign controlled_buffer_1_out = and_24_out ? 1'b0 : 1'bz;  // Controlled_Buffer controlled_buffer_20
  assign {controlled_buffer_2_out_6, controlled_buffer_2_out_5, controlled_buffer_2_out_4, controlled_buffer_2_out_3, controlled_buffer_2_out_2, controlled_buffer_2_out} = and_33_out ? {28'hc400a, multiplexer_7_out} : 30'bz;  // Controlled_Buffer controlled_buffer_21
  assign {controlled_buffer_2_out_6, controlled_buffer_2_out_5, controlled_buffer_2_out_4, controlled_buffer_2_out_3, controlled_buffer_2_out_2, controlled_buffer_2_out} = and_34_out ? 30'h31002c : 30'bz;  // Controlled_Buffer controlled_buffer_22
  Adder #(.width(16)) adder_1 (
    .a(multiplexer_2_out), .b(multiplexer_3_out), .out(adder_1_out), .cin(multiplexer_4_out),
    .cout(adder_1_cout));
  Subtractor #(.width(16)) subtractor_1 (
    .a(multiplexer_2_out), .b(multiplexer_3_out), .out(subtractor_1_out), .bin(multiplexer_5_out),
    .bout(subtractor_1_bout));
  Multiplier #(.width(16)) multiplier_1 (
    .a(multiplexer_2_out), .b(multiplexer_3_out), .out(multiplier_1_out), .cin({16{1'b0}}));  // open: cout
  Divider #(.width(16)) divider_1 (
    .a(multiplexer_2_out), .b(multiplexer_3_out), .out(divider_1_out));  // open: upper, rem
  assign not_3_out = ~multiplexer_2_out;  // NOT_Gate not_3, 16 bits wide
  assign and_25_out = multiplexer_2_out & multiplexer_3_out;  // AND_Gate and_25, 16 bits wide
  assign or_3_out = multiplexer_2_out | multiplexer_3_out;  // OR_Gate or_3, 16 bits wide
  assign xor_2_out = multiplexer_2_out ^ multiplexer_3_out;  // XOR_Gate xor_2, 16 bits wide
  and and_26 (and_26_out, and_54_out, decoder_1_out1);
  assign {controlled_buffer_2_out_6, controlled_buffer_2_out_5, controlled_buffer_2_out_4, controlled_buffer_2_out_3, controlled_buffer_2_out_2, controlled_buffer_2_out} = and_26_out ? {{10{1'b0}}, multiplexer_7_out, 16'h10a, decoder_3_out0[1:0]} : 30'bz;  // Controlled_Buffer controlled_buffer_23
  assign controlled_buffer_1_out = and_26_out ? 1'b0 : 1'bz;  // Controlled_Buffer controlled_buffer_24
  and and_27 (and_27_out, and_55_out, decoder_1_out1);
  assign {controlled_buffer_2_out_6, controlled_buffer_2_out_5, controlled_buffer_2_out_4, controlled_buffer_2_out_3, controlled_buffer_2_out_2, controlled_buffer_2_out} = and_27_out ? {4'b0000, decoder_6_out0, 2'b10, decoder_3_out0[1:0], 18'h25} : 30'bz;  // Controlled_Buffer controlled_buffer_25
  assign controlled_buffer_1_out = and_27_out ? 1'b0 : 1'bz;  // Controlled_Buffer controlled_buffer_26
  and and_28 (and_28_out, and_56_out, decoder_1_out1);
  assign {controlled_buffer_2_out_6, controlled_buffer_2_out_5, controlled_buffer_2_out_4, controlled_buffer_2_out_3, controlled_buffer_2_out_2, controlled_buffer_2_out} = and_28_out ? {4'b0000, multiplexer_7_out_2[25:22], 12'hcbe, multiplexer_7_out_2[9:6], 1'b0, multiplexer_7_out, 1'b0, decoder_3_out0[1:0]} : 30'bz;  // Controlled_Buffer controlled_buffer_27
  assign controlled_buffer_1_out = and_28_out ? 1'b0 : 1'bz;  // Controlled_Buffer controlled_buffer_28
  and and_29 (and_29_out, and_52_out, decoder_1_out1);
  and and_30 (and_30_out, and_29_out, not_4_out);
  assign {controlled_buffer_2_out_6, controlled_buffer_2_out_5, controlled_buffer_2_out_4, controlled_buffer_2_out_3, controlled_buffer_2_out_2, controlled_buffer_2_out} = and_30_out ? 30'h32002d : 30'bz;  // Controlled_Buffer controlled_buffer_29
  assign controlled_buffer_1_out = and_30_out ? 1'b0 : 1'bz;  // Controlled_Buffer controlled_buffer_30
  assign controlled_buffer_1_out = and_33_out ? 1'b0 : 1'bz;  // Controlled_Buffer controlled_buffer_31
  and and_31 (and_31_out, and_53_out, decoder_1_out1);
  and and_32 (and_32_out, and_31_out, not_5_out);
  assign {controlled_buffer_2_out_6, controlled_buffer_2_out_5, controlled_buffer_2_out_4, controlled_buffer_2_out_3, controlled_buffer_2_out_2, controlled_buffer_2_out} = and_32_out ? 30'h32002d : 30'bz;  // Controlled_Buffer controlled_buffer_32
  assign controlled_buffer_1_out = and_32_out ? 1'b0 : 1'bz;  // Controlled_Buffer controlled_buffer_33
  assign controlled_buffer_1_out = and_34_out ? 1'b0 : 1'bz;  // Controlled_Buffer controlled_buffer_34
  Comparator #(.width(16)) comparator_1 (
    .a(multiplexer_2_out), .b(multiplexer_3_out), .gt(comparator_1_gt), .eq(comparator_1_eq),
    .lt(comparator_1_lt));
  assign controlled_buffer_35_out = decoder_5_out0 ? adder_1_cout : 1'bz;  // Controlled_Buffer controlled_buffer_35
  assign controlled_buffer_35_out = decoder_5_out1 ? subtractor_1_bout : 1'bz;  // Controlled_Buffer controlled_buffer_36
  assign controlled_buffer_35_out = decoder_5_out2 ? 1'b0 : 1'bz;  // Controlled_Buffer controlled_buffer_37
  assign controlled_buffer_35_out = decoder_5_out3 ? 1'b0 : 1'bz;  // Controlled_Buffer controlled_buffer_38
  Decoder #(.enable("false"), .select(4)) decoder_5 (
    .out0(decoder_5_out0), .out1(decoder_5_out1), .out2(decoder_5_out2), .out3(decoder_5_out3),
    .out4(decoder_5_out4), .out5(decoder_5_out5), .out6(decoder_5_out6), .out7(decoder_5_out7),
    .out8(decoder_5_out8), .out9(decoder_5_out9), .sel(controlled_buffer_2_out_3));  // open: out10, out11, out12, out13, out14, out15
  assign bit_extender_1_out = {{3{Reset_out}}, Reset_out};  // Bit_Extender bit_extender_1
  and and_33 (and_33_out, and_29_out, or_6_out);
  and and_34 (and_34_out, and_31_out, or_8_out);
  assign or_4_out = bit_extender_1_out | controlled_buffer_2_out_6;  // OR_Gate or_4, 4 bits wide
  Decoder #(.enable("false"), .select(2)) decoder_6 (
    .out0(decoder_6_out0[22]), .out1(decoder_6_out0[23]), .out2(decoder_6_out0[24]),
    .out3(decoder_6_out0[25]), .sel(multiplexer_7_out));
  Decoder #(.enable("false"), .select(2)) decoder_7 (
    .out0(multiplexer_7_out_2[22]), .out1(multiplexer_7_out_2[23]), .out2(multiplexer_7_out_2[24]),
    .out3(multiplexer_7_out_2[25]), .sel(decoder_3_out0[1:0]));
  and and_35 (and_35_out, register_1_q[1], decoder_8_out0);
  and and_36 (and_36_out, register_1_q[0], decoder_8_out1);
  not not_4 (not_4_out, or_6_out);
  and and_37 (and_37_out, register_1_q[1], decoder_9_out0);
  and and_38 (and_38_out, register_1_q[0], decoder_9_out1);
  not not_5 (not_5_out, or_8_out);
  assign controlled_buffer_39_out = decoder_5_out0 ? adder_1_out : 16'bz;  // Controlled_Buffer controlled_buffer_39
  assign controlled_buffer_39_out = decoder_5_out1 ? subtractor_1_out : 16'bz;  // Controlled_Buffer controlled_buffer_40
  assign controlled_buffer_39_out = decoder_5_out2 ? multiplier_1_out : 16'bz;  // Controlled_Buffer controlled_buffer_41
  assign controlled_buffer_39_out = decoder_5_out3 ? divider_1_out : 16'bz;  // Controlled_Buffer controlled_buffer_42
  assign controlled_buffer_35_out = decoder_5_out4 ? multiplexer_2_out[15] : 1'bz;  // Controlled_Buffer controlled_buffer_43
  assign controlled_buffer_39_out = decoder_5_out4 ? {multiplexer_2_out[14:0], 1'b0} : 16'bz;  // Controlled_Buffer controlled_buffer_44
  assign controlled_buffer_39_out = decoder_5_out5 ? {1'b0, multiplexer_2_out[15:1]} : 16'bz;  // Controlled_Buffer controlled_buffer_45
  assign controlled_buffer_35_out = decoder_5_out5 ? multiplexer_2_out[0] : 1'bz;  // Controlled_Buffer controlled_buffer_46
  assign controlled_buffer_39_out = decoder_5_out6 ? not_3_out : 16'bz;  // Controlled_Buffer controlled_buffer_47
  assign controlled_buffer_39_out = decoder_5_out7 ? and_25_out : 16'bz;  // Controlled_Buffer controlled_buffer_48
  assign controlled_buffer_39_out = decoder_5_out8 ? or_3_out : 16'bz;  // Controlled_Buffer controlled_buffer_49
  assign controlled_buffer_39_out = decoder_5_out9 ? xor_2_out : 16'bz;  // Controlled_Buffer controlled_buffer_50
  Decoder #(.enable("false"), .select(3)) decoder_8 (
    .out0(decoder_8_out0), .out1(decoder_8_out1), .out2(decoder_8_out2), .out3(decoder_8_out3),
    .out4(decoder_8_out4), .out5(decoder_8_out5), .sel(multiplexer_7_out_2[8:6]));  // open: out6, out7
  and and_39 (and_39_out, register_1_q[2], decoder_8_out2);
  and and_40 (and_40_out, register_1_q[3], decoder_8_out3);
  and and_41 (and_41_out, decoder_8_out4, register_1_q[4]);
  or or_5 (or_5_out, and_35_out, and_36_out, and_39_out, and_40_out, and_41_out);
  or or_6 (or_6_out, or_5_out, decoder_8_out5);
  Decoder #(.enable("false"), .select(3)) decoder_9 (
    .out0(decoder_9_out0), .out1(decoder_9_out1), .out2(decoder_9_out2), .out3(decoder_9_out3),
    .out4(decoder_9_out4), .out5(decoder_9_out5), .sel(multiplexer_7_out_2[8:6]));  // open: out6, out7
  and and_42 (and_42_out, register_1_q[2], decoder_9_out2);
  and and_43 (and_43_out, register_1_q[3], decoder_9_out3);
  and and_44 (and_44_out, decoder_9_out4, register_1_q[4]);
  or or_7 (or_7_out, and_37_out, and_38_out, and_42_out, and_43_out, and_44_out);
  or or_8 (or_8_out, or_7_out, decoder_9_out5);
  Multiplexer #(.enable("false")) multiplexer_4 (
    .in0(1'b0), .in1(CARRY_IN), .out(multiplexer_4_out), .sel(decoder_5_out0));
  assign controlled_buffer_35_out = or_9_out ? 1'b0 : 1'bz;  // Controlled_Buffer controlled_buffer_51
  or or_9 (or_9_out, decoder_5_out6, decoder_5_out7, decoder_5_out8, decoder_5_out9);
  Multiplexer #(.enable("false")) multiplexer_5 (
    .in0(1'b0), .in1(CARRY_IN), .out(multiplexer_5_out), .sel(decoder_5_out1));
  nor nor_1 (nor_1_out, controlled_buffer_39_out[15], controlled_buffer_39_out[14], controlled_buffer_39_out[13], controlled_buffer_39_out[12], controlled_buffer_39_out[11], controlled_buffer_39_out[10], controlled_buffer_39_out[9], controlled_buffer_39_out[8], controlled_buffer_39_out[7], controlled_buffer_39_out[6], controlled_buffer_39_out[5], controlled_buffer_39_out[4], controlled_buffer_39_out[3], controlled_buffer_39_out[2], controlled_buffer_39_out[1], controlled_buffer_39_out[0]);
  and and_45 (and_45_out, and_51_out, decoder_1_out2);
  assign {controlled_buffer_2_out_6, controlled_buffer_2_out_5, controlled_buffer_2_out_4, controlled_buffer_2_out_3, controlled_buffer_2_out_2, controlled_buffer_2_out} = and_45_out ? 30'h320025 : 30'bz;  // Controlled_Buffer controlled_buffer_52
  assign controlled_buffer_1_out = and_45_out ? 1'b1 : 1'bz;  // Controlled_Buffer controlled_buffer_53
  and and_46 (and_46_out, and_54_out, decoder_1_out2);
  assign {controlled_buffer_2_out_6, controlled_buffer_2_out_5, controlled_buffer_2_out_4, controlled_buffer_2_out_3, controlled_buffer_2_out_2, controlled_buffer_2_out} = and_46_out ? 30'h320025 : 30'bz;  // Controlled_Buffer controlled_buffer_54
  assign controlled_buffer_1_out = and_46_out ? 1'b1 : 1'bz;  // Controlled_Buffer controlled_buffer_55
  and and_47 (and_47_out, and_55_out, decoder_1_out2);
  assign {controlled_buffer_2_out_6, controlled_buffer_2_out_5, controlled_buffer_2_out_4, controlled_buffer_2_out_3, controlled_buffer_2_out_2, controlled_buffer_2_out} = and_47_out ? 30'h320025 : 30'bz;  // Controlled_Buffer controlled_buffer_56
  assign controlled_buffer_1_out = and_47_out ? 1'b1 : 1'bz;  // Controlled_Buffer controlled_buffer_57
  and and_48 (and_48_out, and_56_out, decoder_1_out2);
  assign {controlled_buffer_2_out_6, controlled_buffer_2_out_5, controlled_buffer_2_out_4, controlled_buffer_2_out_3, controlled_buffer_2_out_2, controlled_buffer_2_out} = and_48_out ? 30'h320025 : 30'bz;  // Controlled_Buffer controlled_buffer_58
  assign controlled_buffer_1_out = and_48_out ? 1'b1 : 1'bz;  // Controlled_Buffer controlled_buffer_59
  and and_49 (and_49_out, and_52_out, decoder_1_out2);
  assign {controlled_buffer_2_out_6, controlled_buffer_2_out_5, controlled_buffer_2_out_4, controlled_buffer_2_out_3, controlled_buffer_2_out_2, controlled_buffer_2_out} = and_49_out ? 30'h320025 : 30'bz;  // Controlled_Buffer controlled_buffer_60
  assign controlled_buffer_1_out = and_49_out ? 1'b1 : 1'bz;  // Controlled_Buffer controlled_buffer_61
  and and_50 (and_50_out, and_53_out, decoder_1_out2);
  assign {controlled_buffer_2_out_6, controlled_buffer_2_out_5, controlled_buffer_2_out_4, controlled_buffer_2_out_3, controlled_buffer_2_out_2, controlled_buffer_2_out} = and_50_out ? 30'h320025 : 30'bz;  // Controlled_Buffer controlled_buffer_62
  assign controlled_buffer_1_out = and_50_out ? 1'b1 : 1'bz;  // Controlled_Buffer controlled_buffer_63
  Register #(.width(1)) register_1 (
    .D(comparator_1_gt), .en(controlled_buffer_2_out_4[11]), .clk(not_1_out), .Q(register_1_q[0]),
    .clr(Reset_out));
  Counter #(.max('hffff), .width(16)) counter_2 (
    .load(controlled_buffer_2_out_4[16]), .D(controlled_buffer_39_out),
    .count(controlled_buffer_2_out_4[17]), .Q(counter_2_q), .up(1'b1), .clk(not_1_out), .clr(Reset_out));  // open: carry
  Register #(.width(1)) register_2 (
    .D(comparator_1_eq), .en(controlled_buffer_2_out_4[12]), .clk(not_1_out), .Q(register_1_q[1]),
    .clr(Reset_out));
  Register #(.width(1)) register_3 (
    .D(comparator_1_lt), .en(controlled_buffer_2_out_4[13]), .clk(not_1_out), .Q(register_1_q[2]),
    .clr(Reset_out));
  Register #(.width(1)) register_4 (
    .D(nor_1_out), .en(controlled_buffer_2_out_4[14]), .clk(not_1_out), .Q(register_1_q[3]), .clr(Reset_out));
  Multiplexer #(.enable("false"), .select(3), .width(16)) multiplexer_6 (
    .in0(R0_2_q), .in1(R1_2_q), .in2(R2_2_q), .in3(R3_2_q), .in4(counter_2_q), .in5(multiplexer_2_out),
    .in6(multiplexer_3_out), .out(multiplexer_6_out), .sel(controlled_buffer_2_out_4[20:18]));  // open: in7
  Register #(.width(1)) register_5 (
    .D(controlled_buffer_35_out), .en(controlled_buffer_2_out_4[15]), .clk(not_1_out), .Q(register_1_q[4]),
    .clr(Reset_out));
  assign controlled_buffer_64_out = controlled_buffer_2_out_4[10] ? controlled_buffer_39_out : 16'bz;  // Controlled_Buffer controlled_buffer_64
  RAM_part #(.addrWidth(16), .dataWidth(16), .databus("bidir")) ram_1 (
    .addr(multiplexer_6_out), .we(1'b1), .oe(controlled_buffer_2_out_4[21]), .clk(not_1_out),
    .data(controlled_buffer_64_out));
  Register #(.trigger("falling"), .width(16)) register_6 (
    .D(controlled_buffer_64_out), .en(decoder_1_out0), .clk(not_1_out), .Q(register_6_q), .clr(Reset_out));
  and and_51 (and_51_out, ~multiplexer_7_out_3[9], ~multiplexer_7_out_3[10], ~multiplexer_7_out_3[11], ~multiplexer_7_out_3[12], ~multiplexer_7_out_3[13], ~multiplexer_7_out_3[14], ~multiplexer_7_out_3[15]);  // AND_Gate
  and and_52 (and_52_out, ~multiplexer_7_out_2[9], multiplexer_7_out_3[8], ~multiplexer_7_out_3[9], multiplexer_7_out_3[10], ~multiplexer_7_out_3[11], ~multiplexer_7_out_3[12], ~multiplexer_7_out_3[13], ~multiplexer_7_out_3[14], ~multiplexer_7_out_3[15]);  // AND_Gate
  and and_53 (and_53_out, multiplexer_7_out_2[9], multiplexer_7_out_3[8], ~multiplexer_7_out_3[9], multiplexer_7_out_3[10], ~multiplexer_7_out_3[11], ~multiplexer_7_out_3[12], ~multiplexer_7_out_3[13], ~multiplexer_7_out_3[14], ~multiplexer_7_out_3[15]);  // AND_Gate
  and and_54 (and_54_out, multiplexer_7_out_3[8], multiplexer_7_out_3[9], ~multiplexer_7_out_3[10], ~multiplexer_7_out_3[11], ~multiplexer_7_out_3[12], ~multiplexer_7_out_3[13], ~multiplexer_7_out_3[14], ~multiplexer_7_out_3[15]);  // AND_Gate
  and and_55 (and_55_out, ~multiplexer_7_out_3[8], multiplexer_7_out_3[9], ~multiplexer_7_out_3[10], ~multiplexer_7_out_3[11], ~multiplexer_7_out_3[12], ~multiplexer_7_out_3[13], ~multiplexer_7_out_3[14], ~multiplexer_7_out_3[15]);  // AND_Gate
  and and_56 (and_56_out, ~multiplexer_7_out_3[8], ~multiplexer_7_out_3[9], multiplexer_7_out_3[10], ~multiplexer_7_out_3[11], ~multiplexer_7_out_3[12], ~multiplexer_7_out_3[13], ~multiplexer_7_out_3[14], ~multiplexer_7_out_3[15]);  // AND_Gate
  and and_57 (and_57_out, multiplexer_7_out_3[8], multiplexer_7_out_3[9], multiplexer_7_out_3[10], ~multiplexer_7_out_3[11], ~multiplexer_7_out_3[12], ~multiplexer_7_out_3[13], ~multiplexer_7_out_3[14], ~multiplexer_7_out_3[15]);  // AND_Gate
  and and_58 (and_58_out, multiplexer_7_out_3[15], ~multiplexer_7_out_3[14], multiplexer_7_out_3[13], ~multiplexer_7_out_3[12], multiplexer_7_out_3[11], ~multiplexer_7_out_3[10], multiplexer_7_out_3[9], ~multiplexer_7_out_3[8], multiplexer_7_out_2[9], ~multiplexer_7_out_2[8], multiplexer_7_out_2[7], ~multiplexer_7_out_2[6], decoder_3_out0[1], ~decoder_3_out0[0], multiplexer_7_out[1], ~multiplexer_7_out[0]);  // AND_Gate
  Multiplexer #(.enable("false"), .width(16)) multiplexer_7 (
    .in0(register_6_q), .in1(16'haaaa),
    .out({multiplexer_7_out_3, multiplexer_7_out_2[9:6], decoder_3_out0[1:0], multiplexer_7_out}),
    .sel(Reset_out));

  // Notes on the sheet:
  //   Press [CTRL + K] to start or stop the Clock
  //   Welcome to Heza 1 Processor
  //   Welcome to the Logisim Evolution version of the Heza 1 CPU.
  //   To learn more about it, see the User Manual.
  //   To start coding a program for the Heza 1 processor, please refer to the Instruction Table.
  //   Press [CTRL + R] to reset the simulation
  //   Select the Hand icon from the topbar to start toggling buttons
  //   You can choose your clock speed from the top menu ("Simulate" > "Tick Frequency" > ...)
  //   Flags
endmodule

module RAM (
  input  [15:0] RAM_INPUT__i,
  input  RAM_LD__i,
  input  CLK__i,
  output [15:0] RAM_OUTPUT__o
);

  RAM_part #(.addrWidth(16), .dataWidth(16), .databus("bidir")) ram_1 (
    .addr(RAM_INPUT__i), .we(1'b1), .oe(RAM_LD__i), .clk(CLK__i), .data(RAM_OUTPUT__o));
endmodule

module CIRC (
  input  CARRY_IN__i,
  input  RESET__i,
  input  CLK__i,
  input  [15:0] D_Bus__i,
  output [15:0] D_Bus__o,
  output [15:0] ALU_Bus__o,
  output [15:0] IP__o,
  output [15:0] IR__o,
  output FLAG_____o,
  output END__o,
  output [15:0] R0__o,
  output [15:0] R1__o,
  output [15:0] R2__o,
  output [15:0] R3__o,
  output FLAG_____o_2,
  output FLAG_____o_3,
  output FLAG__z__o,
  output FLAG__c__o,
  output [15:0] RAM_INPUT__o,
  output RAM_LD__o
);

  wire adder_1_cout, and_1_out, and_2_out, and_3_out, and_4_out, and_5_out, and_6_out, and_7_out, and_8_out,
       and_10_out, and_11_out, and_13_out, and_14_out, and_16_out, and_17_out, and_18_out, and_20_out,
       and_21_out, and_22_out, and_24_out, and_26_out, and_27_out, and_28_out, and_29_out, and_30_out,
       and_31_out, and_32_out, and_33_out, and_34_out, and_35_out, and_36_out, and_37_out, and_38_out,
       and_39_out, and_40_out, and_41_out, and_42_out, and_43_out, and_44_out, and_45_out, and_46_out,
       and_47_out, and_48_out, and_49_out, and_50_out, and_51_out, and_52_out, and_53_out, and_54_out,
       and_55_out, and_56_out, and_57_out, and_58_out, comparator_1_eq, comparator_1_gt, comparator_1_lt,
       controlled_buffer_1_out, controlled_buffer_35_out, d_ff_1_q, decoder_1_out0, decoder_1_out1,
       decoder_1_out2, decoder_1_out3, decoder_1_out4, decoder_5_out0, decoder_5_out1, decoder_5_out2,
       decoder_5_out3, decoder_5_out4, decoder_5_out5, decoder_5_out6, decoder_5_out7, decoder_5_out8,
       decoder_5_out9, decoder_8_out0, decoder_8_out1, decoder_8_out2, decoder_8_out3, decoder_8_out4,
       decoder_8_out5, decoder_9_out0, decoder_9_out1, decoder_9_out2, decoder_9_out3, decoder_9_out4,
       decoder_9_out5, multiplexer_4_out, multiplexer_5_out, nor_1_out, not_1_out, not_2_out, not_4_out,
       not_5_out, or_1_out, or_2_out, or_5_out, or_6_out, or_7_out, or_8_out, or_9_out, subtractor_1_bout,
       xor_1_out;
  wire [1:0] multiplexer_7_out;
  wire [2:0] controlled_buffer_2_out, controlled_buffer_2_out_2, counter_1_q;
  wire [3:0] bit_extender_1_out, controlled_buffer_2_out_3, controlled_buffer_2_out_5,
       controlled_buffer_2_out_6, decoder_4_out0, or_4_out;
  wire [15:0] adder_1_out, and_25_out, divider_1_out, multiplexer_2_out, multiplexer_3_out, multiplier_1_out,
       not_3_out, or_3_out, subtractor_1_out, xor_2_out;
  wire [15:8] multiplexer_7_out_3;
  wire [20:10] controlled_buffer_2_out_4;
  wire [25:6] multiplexer_7_out_2;
  wire [25:22] and_12_out, decoder_6_out0;
  wire [29:0] decoder_3_out0;
  wire [29:26] decoder_2_out0;

  Counter #(.max('h7), .width(3)) counter_1 (
    .load(1'b0), .count(1'b1), .Q(counter_1_q), .up(1'b1), .clk(not_1_out), .clr(or_1_out));  // open: D, carry
  or or_1 (or_1_out, RESET__i, decoder_1_out4, controlled_buffer_1_out);
  Decoder #(.enable("false"), .select(3)) decoder_1 (
    .out0(decoder_1_out0), .out1(decoder_1_out1), .out2(decoder_1_out2), .out3(decoder_1_out3),
    .out4(decoder_1_out4), .sel(counter_1_q));  // open: out5, out6, out7
  D_Flip_Flop d_ff_1 (.clk(RESET__i), .D(CLK__i), .Q(d_ff_1_q));  // open: Qn, preset, reset
  xor xor_1 (xor_1_out, d_ff_1_q, CLK__i);
  not not_1 (not_1_out, xor_1_out);
  Register #(.width(16)) R0 (
    .D(ALU_Bus__o), .en(controlled_buffer_2_out_5[0]), .clk(not_1_out), .Q(R0__o), .clr(or_4_out[0]));
  Register #(.width(16)) R1 (
    .D(ALU_Bus__o), .en(controlled_buffer_2_out_5[1]), .clk(not_1_out), .Q(R1__o), .clr(or_4_out[1]));
  Register #(.width(16)) R2 (
    .D(ALU_Bus__o), .en(controlled_buffer_2_out_5[2]), .clk(not_1_out), .Q(R2__o), .clr(or_4_out[2]));
  Register #(.width(16)) R3 (
    .D(ALU_Bus__o), .en(controlled_buffer_2_out_5[3]), .clk(not_1_out), .Q(R3__o), .clr(or_4_out[3]));
  and and_1 (and_1_out, and_51_out, decoder_1_out0);
  and and_2 (and_2_out, and_1_out, not_2_out);
  not not_2 (not_2_out, and_20_out);
  assign controlled_buffer_1_out = and_2_out ? 1'b1 : 1'bz;  // Controlled_Buffer controlled_buffer_1
  and and_3 (and_3_out, and_54_out, decoder_1_out0);
  assign {controlled_buffer_2_out_6, controlled_buffer_2_out_5, RAM_LD__o, controlled_buffer_2_out_4, controlled_buffer_2_out_3, controlled_buffer_2_out_2, controlled_buffer_2_out} = and_3_out ? 30'h32002d : 30'bz;  // Controlled_Buffer controlled_buffer_2
  and and_4 (and_4_out, and_55_out, decoder_1_out0);
  assign {controlled_buffer_2_out_6, controlled_buffer_2_out_5, RAM_LD__o, controlled_buffer_2_out_4, controlled_buffer_2_out_3, controlled_buffer_2_out_2, controlled_buffer_2_out} = and_4_out ? 30'h32002d : 30'bz;  // Controlled_Buffer controlled_buffer_3
  and and_5 (and_5_out, and_56_out, decoder_1_out0);
  assign {controlled_buffer_2_out_6, controlled_buffer_2_out_5, RAM_LD__o, controlled_buffer_2_out_4, controlled_buffer_2_out_3, controlled_buffer_2_out_2, controlled_buffer_2_out} = and_5_out ? 30'h30002d : 30'bz;  // Controlled_Buffer controlled_buffer_4
  and and_6 (and_6_out, and_57_out, decoder_1_out0);
  assign {controlled_buffer_2_out_6, controlled_buffer_2_out_5, RAM_LD__o, controlled_buffer_2_out_4, controlled_buffer_2_out_3, controlled_buffer_2_out_2, controlled_buffer_2_out} = and_6_out ? {decoder_2_out0, 26'h32002d} : 30'bz;  // Controlled_Buffer controlled_buffer_5
  and and_7 (and_7_out, and_52_out, decoder_1_out0);
  assign {controlled_buffer_2_out_6, controlled_buffer_2_out_5, RAM_LD__o, controlled_buffer_2_out_4, controlled_buffer_2_out_3, controlled_buffer_2_out_2, controlled_buffer_2_out} = and_7_out ? 30'h30002d : 30'bz;  // Controlled_Buffer controlled_buffer_6
  and and_8 (and_8_out, and_53_out, decoder_1_out0);
  assign {controlled_buffer_2_out_6, controlled_buffer_2_out_5, RAM_LD__o, controlled_buffer_2_out_4, controlled_buffer_2_out_3, controlled_buffer_2_out_2, controlled_buffer_2_out} = and_8_out ? 30'h32002d : 30'bz;  // Controlled_Buffer controlled_buffer_7
  and and_9 (END__o, and_58_out, decoder_1_out0);
  assign {controlled_buffer_2_out_6, controlled_buffer_2_out_5, RAM_LD__o, controlled_buffer_2_out_4, controlled_buffer_2_out_3, controlled_buffer_2_out_2, controlled_buffer_2_out} = END__o ? 30'h30002d : 30'bz;  // Controlled_Buffer controlled_buffer_8
  assign controlled_buffer_1_out = END__o ? 1'b1 : 1'bz;  // Controlled_Buffer controlled_buffer_9
  assign {controlled_buffer_2_out_6, controlled_buffer_2_out_5, RAM_LD__o, controlled_buffer_2_out_4, controlled_buffer_2_out_3, controlled_buffer_2_out_2, controlled_buffer_2_out} = and_2_out ? {decoder_3_out0[29:22], 20'hc800a, decoder_3_out0[1:0]} : 30'bz;  // Controlled_Buffer controlled_buffer_10
  assign controlled_buffer_1_out = and_3_out ? 1'b0 : 1'bz;  // Controlled_Buffer controlled_buffer_11
  assign controlled_buffer_1_out = and_4_out ? 1'b0 : 1'bz;  // Controlled_Buffer controlled_buffer_12
  assign controlled_buffer_1_out = and_5_out ? 1'b0 : 1'bz;  // Controlled_Buffer controlled_buffer_13
  assign controlled_buffer_1_out = and_6_out ? 1'b1 : 1'bz;  // Controlled_Buffer controlled_buffer_14
  assign controlled_buffer_1_out = and_7_out ? 1'b0 : 1'bz;  // Controlled_Buffer controlled_buffer_15
  assign controlled_buffer_1_out = and_8_out ? 1'b0 : 1'bz;  // Controlled_Buffer controlled_buffer_16
  Multiplexer #(.enable("false"), .width(4)) multiplexer_1 (
    .in0(4'b0000), .in1(decoder_4_out0), .out(decoder_3_out0[29:26]), .sel(and_10_out));
  Decoder #(.enable("false"), .select(2)) decoder_2 (
    .out0(decoder_2_out0[26]), .out1(decoder_2_out0[27]), .out2(decoder_2_out0[28]),
    .out3(decoder_2_out0[29]), .sel(multiplexer_7_out));
  and and_10 (and_10_out, and_1_out, multiplexer_7_out_3[8]);
  and and_11 (and_11_out, ~multiplexer_7_out[0], ~decoder_3_out0[0]);  // AND_Gate
  and and_12 (and_12_out[22], and_11_out, and_13_out);
  Decoder #(.enable("false"), .select(2)) decoder_3 (
    .out0(decoder_3_out0[22]), .out1(decoder_3_out0[23]), .out2(decoder_3_out0[24]),
    .out3(decoder_3_out0[25]), .sel(multiplexer_7_out));
  Decoder #(.enable("false"), .select(2)) decoder_4 (
    .out0(decoder_4_out0[0]), .out1(decoder_4_out0[1]), .out2(decoder_4_out0[2]), .out3(decoder_4_out0[3]),
    .sel(decoder_3_out0[1:0]));
  and and_13 (and_13_out, ~multiplexer_7_out[1], ~decoder_3_out0[1]);  // AND_Gate
  and and_14 (and_14_out, multiplexer_7_out[0], decoder_3_out0[0]);
  and and_15 (and_12_out[23], and_14_out, and_16_out);
  and and_16 (and_16_out, ~multiplexer_7_out[1], ~decoder_3_out0[1]);  // AND_Gate
  and and_17 (and_17_out, ~multiplexer_7_out[0], ~decoder_3_out0[0]);  // AND_Gate
  and and_18 (and_18_out, multiplexer_7_out[1], decoder_3_out0[1]);
  and and_19 (and_12_out[24], and_17_out, and_18_out);
  or or_2 (or_2_out, and_12_out[22], and_12_out[23], and_12_out[24], and_12_out[25]);
  and and_20 (and_20_out, and_1_out, or_2_out);
  assign {controlled_buffer_2_out_6, controlled_buffer_2_out_5, RAM_LD__o, controlled_buffer_2_out_4, controlled_buffer_2_out_3, controlled_buffer_2_out_2, controlled_buffer_2_out} = and_20_out ? 30'h32002d : 30'bz;  // Controlled_Buffer controlled_buffer_17
  assign controlled_buffer_1_out = and_20_out ? 1'b0 : 1'bz;  // Controlled_Buffer controlled_buffer_18
  and and_21 (and_21_out, multiplexer_7_out[0], decoder_3_out0[0]);
  and and_22 (and_22_out, multiplexer_7_out[1], decoder_3_out0[1]);
  and and_23 (and_12_out[25], and_21_out, and_22_out);
  Multiplexer #(.enable("false"), .select(3), .width(16)) multiplexer_2 (
    .in0(R0__o), .in1(R1__o), .in2(R2__o), .in3(R3__o), .in4(D_Bus__i), .in5({16{1'b0}}),
    .out(multiplexer_2_out), .sel(controlled_buffer_2_out));  // open: in6, in7
  Multiplexer #(.enable("false"), .select(3), .width(16)) multiplexer_3 (
    .in0(R0__o), .in1(R1__o), .in2(R2__o), .in3(R3__o), .in4(D_Bus__i), .in5({16{1'b0}}),
    .out(multiplexer_3_out), .sel(controlled_buffer_2_out_2));  // open: in6, in7
  and and_24 (and_24_out, and_51_out, decoder_1_out1);
  assign {controlled_buffer_2_out_6, controlled_buffer_2_out_5, RAM_LD__o, controlled_buffer_2_out_4, controlled_buffer_2_out_3, controlled_buffer_2_out_2, controlled_buffer_2_out} = and_24_out ? {4'b0000, and_12_out, 22'h320025} : 30'bz;  // Controlled_Buffer controlled_buffer_19
  assign controlled_buffer_1_out = and_24_out ? 1'b0 : 1'bz;  // Controlled_Buffer controlled_buffer_20
  assign {controlled_buffer_2_out_6, controlled_buffer_2_out_5, RAM_LD__o, controlled_buffer_2_out_4, controlled_buffer_2_out_3, controlled_buffer_2_out_2, controlled_buffer_2_out} = and_33_out ? {28'hc400a, multiplexer_7_out} : 30'bz;  // Controlled_Buffer controlled_buffer_21
  assign {controlled_buffer_2_out_6, controlled_buffer_2_out_5, RAM_LD__o, controlled_buffer_2_out_4, controlled_buffer_2_out_3, controlled_buffer_2_out_2, controlled_buffer_2_out} = and_34_out ? 30'h31002c : 30'bz;  // Controlled_Buffer controlled_buffer_22
  Adder #(.width(16)) adder_1 (
    .a(multiplexer_2_out), .b(multiplexer_3_out), .out(adder_1_out), .cin(multiplexer_4_out),
    .cout(adder_1_cout));
  Subtractor #(.width(16)) subtractor_1 (
    .a(multiplexer_2_out), .b(multiplexer_3_out), .out(subtractor_1_out), .bin(multiplexer_5_out),
    .bout(subtractor_1_bout));
  Multiplier #(.width(16)) multiplier_1 (
    .a(multiplexer_2_out), .b(multiplexer_3_out), .out(multiplier_1_out), .cin({16{1'b0}}));  // open: cout
  Divider #(.width(16)) divider_1 (
    .a(multiplexer_2_out), .b(multiplexer_3_out), .out(divider_1_out));  // open: upper, rem
  assign not_3_out = ~multiplexer_2_out;  // NOT_Gate not_3, 16 bits wide
  assign and_25_out = multiplexer_2_out & multiplexer_3_out;  // AND_Gate and_25, 16 bits wide
  assign or_3_out = multiplexer_2_out | multiplexer_3_out;  // OR_Gate or_3, 16 bits wide
  assign xor_2_out = multiplexer_2_out ^ multiplexer_3_out;  // XOR_Gate xor_2, 16 bits wide
  and and_26 (and_26_out, and_54_out, decoder_1_out1);
  assign {controlled_buffer_2_out_6, controlled_buffer_2_out_5, RAM_LD__o, controlled_buffer_2_out_4, controlled_buffer_2_out_3, controlled_buffer_2_out_2, controlled_buffer_2_out} = and_26_out ? {{10{1'b0}}, multiplexer_7_out, 16'h10a, decoder_3_out0[1:0]} : 30'bz;  // Controlled_Buffer controlled_buffer_23
  assign controlled_buffer_1_out = and_26_out ? 1'b0 : 1'bz;  // Controlled_Buffer controlled_buffer_24
  and and_27 (and_27_out, and_55_out, decoder_1_out1);
  assign {controlled_buffer_2_out_6, controlled_buffer_2_out_5, RAM_LD__o, controlled_buffer_2_out_4, controlled_buffer_2_out_3, controlled_buffer_2_out_2, controlled_buffer_2_out} = and_27_out ? {4'b0000, decoder_6_out0, 2'b10, decoder_3_out0[1:0], 18'h25} : 30'bz;  // Controlled_Buffer controlled_buffer_25
  assign controlled_buffer_1_out = and_27_out ? 1'b0 : 1'bz;  // Controlled_Buffer controlled_buffer_26
  and and_28 (and_28_out, and_56_out, decoder_1_out1);
  assign {controlled_buffer_2_out_6, controlled_buffer_2_out_5, RAM_LD__o, controlled_buffer_2_out_4, controlled_buffer_2_out_3, controlled_buffer_2_out_2, controlled_buffer_2_out} = and_28_out ? {4'b0000, multiplexer_7_out_2[25:22], 12'hcbe, multiplexer_7_out_2[9:6], 1'b0, multiplexer_7_out, 1'b0, decoder_3_out0[1:0]} : 30'bz;  // Controlled_Buffer controlled_buffer_27
  assign controlled_buffer_1_out = and_28_out ? 1'b0 : 1'bz;  // Controlled_Buffer controlled_buffer_28
  and and_29 (and_29_out, and_52_out, decoder_1_out1);
  and and_30 (and_30_out, and_29_out, not_4_out);
  assign {controlled_buffer_2_out_6, controlled_buffer_2_out_5, RAM_LD__o, controlled_buffer_2_out_4, controlled_buffer_2_out_3, controlled_buffer_2_out_2, controlled_buffer_2_out} = and_30_out ? 30'h32002d : 30'bz;  // Controlled_Buffer controlled_buffer_29
  assign controlled_buffer_1_out = and_30_out ? 1'b0 : 1'bz;  // Controlled_Buffer controlled_buffer_30
  assign controlled_buffer_1_out = and_33_out ? 1'b0 : 1'bz;  // Controlled_Buffer controlled_buffer_31
  and and_31 (and_31_out, and_53_out, decoder_1_out1);
  and and_32 (and_32_out, and_31_out, not_5_out);
  assign {controlled_buffer_2_out_6, controlled_buffer_2_out_5, RAM_LD__o, controlled_buffer_2_out_4, controlled_buffer_2_out_3, controlled_buffer_2_out_2, controlled_buffer_2_out} = and_32_out ? 30'h32002d : 30'bz;  // Controlled_Buffer controlled_buffer_32
  assign controlled_buffer_1_out = and_32_out ? 1'b0 : 1'bz;  // Controlled_Buffer controlled_buffer_33
  assign controlled_buffer_1_out = and_34_out ? 1'b0 : 1'bz;  // Controlled_Buffer controlled_buffer_34
  Comparator #(.width(16)) comparator_1 (
    .a(multiplexer_2_out), .b(multiplexer_3_out), .gt(comparator_1_gt), .eq(comparator_1_eq),
    .lt(comparator_1_lt));
  assign controlled_buffer_35_out = decoder_5_out0 ? adder_1_cout : 1'bz;  // Controlled_Buffer controlled_buffer_35
  assign controlled_buffer_35_out = decoder_5_out1 ? subtractor_1_bout : 1'bz;  // Controlled_Buffer controlled_buffer_36
  assign controlled_buffer_35_out = decoder_5_out2 ? 1'b0 : 1'bz;  // Controlled_Buffer controlled_buffer_37
  assign controlled_buffer_35_out = decoder_5_out3 ? 1'b0 : 1'bz;  // Controlled_Buffer controlled_buffer_38
  Decoder #(.enable("false"), .select(4)) decoder_5 (
    .out0(decoder_5_out0), .out1(decoder_5_out1), .out2(decoder_5_out2), .out3(decoder_5_out3),
    .out4(decoder_5_out4), .out5(decoder_5_out5), .out6(decoder_5_out6), .out7(decoder_5_out7),
    .out8(decoder_5_out8), .out9(decoder_5_out9), .sel(controlled_buffer_2_out_3));  // open: out10, out11, out12, out13, out14, out15
  assign bit_extender_1_out = {{3{RESET__i}}, RESET__i};  // Bit_Extender bit_extender_1
  and and_33 (and_33_out, and_29_out, or_6_out);
  and and_34 (and_34_out, and_31_out, or_8_out);
  assign or_4_out = bit_extender_1_out | controlled_buffer_2_out_6;  // OR_Gate or_4, 4 bits wide
  Decoder #(.enable("false"), .select(2)) decoder_6 (
    .out0(decoder_6_out0[22]), .out1(decoder_6_out0[23]), .out2(decoder_6_out0[24]),
    .out3(decoder_6_out0[25]), .sel(multiplexer_7_out));
  Decoder #(.enable("false"), .select(2)) decoder_7 (
    .out0(multiplexer_7_out_2[22]), .out1(multiplexer_7_out_2[23]), .out2(multiplexer_7_out_2[24]),
    .out3(multiplexer_7_out_2[25]), .sel(decoder_3_out0[1:0]));
  and and_35 (and_35_out, FLAG_____o_2, decoder_8_out0);
  and and_36 (and_36_out, FLAG_____o, decoder_8_out1);
  not not_4 (not_4_out, or_6_out);
  and and_37 (and_37_out, FLAG_____o_2, decoder_9_out0);
  and and_38 (and_38_out, FLAG_____o, decoder_9_out1);
  not not_5 (not_5_out, or_8_out);
  assign ALU_Bus__o = decoder_5_out0 ? adder_1_out : 16'bz;  // Controlled_Buffer controlled_buffer_39
  assign ALU_Bus__o = decoder_5_out1 ? subtractor_1_out : 16'bz;  // Controlled_Buffer controlled_buffer_40
  assign ALU_Bus__o = decoder_5_out2 ? multiplier_1_out : 16'bz;  // Controlled_Buffer controlled_buffer_41
  assign ALU_Bus__o = decoder_5_out3 ? divider_1_out : 16'bz;  // Controlled_Buffer controlled_buffer_42
  assign controlled_buffer_35_out = decoder_5_out4 ? multiplexer_2_out[15] : 1'bz;  // Controlled_Buffer controlled_buffer_43
  assign ALU_Bus__o = decoder_5_out4 ? {multiplexer_2_out[14:0], 1'b0} : 16'bz;  // Controlled_Buffer controlled_buffer_44
  assign ALU_Bus__o = decoder_5_out5 ? {1'b0, multiplexer_2_out[15:1]} : 16'bz;  // Controlled_Buffer controlled_buffer_45
  assign controlled_buffer_35_out = decoder_5_out5 ? multiplexer_2_out[0] : 1'bz;  // Controlled_Buffer controlled_buffer_46
  assign ALU_Bus__o = decoder_5_out6 ? not_3_out : 16'bz;  // Controlled_Buffer controlled_buffer_47
  assign ALU_Bus__o = decoder_5_out7 ? and_25_out : 16'bz;  // Controlled_Buffer controlled_buffer_48
  assign ALU_Bus__o = decoder_5_out8 ? or_3_out : 16'bz;  // Controlled_Buffer controlled_buffer_49
  assign ALU_Bus__o = decoder_5_out9 ? xor_2_out : 16'bz;  // Controlled_Buffer controlled_buffer_50
  Decoder #(.enable("false"), .select(3)) decoder_8 (
    .out0(decoder_8_out0), .out1(decoder_8_out1), .out2(decoder_8_out2), .out3(decoder_8_out3),
    .out4(decoder_8_out4), .out5(decoder_8_out5), .sel(multiplexer_7_out_2[8:6]));  // open: out6, out7
  and and_39 (and_39_out, FLAG_____o_3, decoder_8_out2);
  and and_40 (and_40_out, FLAG__z__o, decoder_8_out3);
  and and_41 (and_41_out, decoder_8_out4, FLAG__c__o);
  or or_5 (or_5_out, and_35_out, and_36_out, and_39_out, and_40_out, and_41_out);
  or or_6 (or_6_out, or_5_out, decoder_8_out5);
  Decoder #(.enable("false"), .select(3)) decoder_9 (
    .out0(decoder_9_out0), .out1(decoder_9_out1), .out2(decoder_9_out2), .out3(decoder_9_out3),
    .out4(decoder_9_out4), .out5(decoder_9_out5), .sel(multiplexer_7_out_2[8:6]));  // open: out6, out7
  and and_42 (and_42_out, FLAG_____o_3, decoder_9_out2);
  and and_43 (and_43_out, FLAG__z__o, decoder_9_out3);
  and and_44 (and_44_out, decoder_9_out4, FLAG__c__o);
  or or_7 (or_7_out, and_37_out, and_38_out, and_42_out, and_43_out, and_44_out);
  or or_8 (or_8_out, or_7_out, decoder_9_out5);
  Multiplexer #(.enable("false")) multiplexer_4 (
    .in0(1'b0), .in1(CARRY_IN__i), .out(multiplexer_4_out), .sel(decoder_5_out0));
  assign controlled_buffer_35_out = or_9_out ? 1'b0 : 1'bz;  // Controlled_Buffer controlled_buffer_51
  or or_9 (or_9_out, decoder_5_out6, decoder_5_out7, decoder_5_out8, decoder_5_out9);
  Multiplexer #(.enable("false")) multiplexer_5 (
    .in0(1'b0), .in1(CARRY_IN__i), .out(multiplexer_5_out), .sel(decoder_5_out1));
  nor nor_1 (nor_1_out, ALU_Bus__o[15], ALU_Bus__o[14], ALU_Bus__o[13], ALU_Bus__o[12], ALU_Bus__o[11], ALU_Bus__o[10], ALU_Bus__o[9], ALU_Bus__o[8], ALU_Bus__o[7], ALU_Bus__o[6], ALU_Bus__o[5], ALU_Bus__o[4], ALU_Bus__o[3], ALU_Bus__o[2], ALU_Bus__o[1], ALU_Bus__o[0]);
  and and_45 (and_45_out, and_51_out, decoder_1_out2);
  assign {controlled_buffer_2_out_6, controlled_buffer_2_out_5, RAM_LD__o, controlled_buffer_2_out_4, controlled_buffer_2_out_3, controlled_buffer_2_out_2, controlled_buffer_2_out} = and_45_out ? 30'h320025 : 30'bz;  // Controlled_Buffer controlled_buffer_52
  assign controlled_buffer_1_out = and_45_out ? 1'b1 : 1'bz;  // Controlled_Buffer controlled_buffer_53
  and and_46 (and_46_out, and_54_out, decoder_1_out2);
  assign {controlled_buffer_2_out_6, controlled_buffer_2_out_5, RAM_LD__o, controlled_buffer_2_out_4, controlled_buffer_2_out_3, controlled_buffer_2_out_2, controlled_buffer_2_out} = and_46_out ? 30'h320025 : 30'bz;  // Controlled_Buffer controlled_buffer_54
  assign controlled_buffer_1_out = and_46_out ? 1'b1 : 1'bz;  // Controlled_Buffer controlled_buffer_55
  and and_47 (and_47_out, and_55_out, decoder_1_out2);
  assign {controlled_buffer_2_out_6, controlled_buffer_2_out_5, RAM_LD__o, controlled_buffer_2_out_4, controlled_buffer_2_out_3, controlled_buffer_2_out_2, controlled_buffer_2_out} = and_47_out ? 30'h320025 : 30'bz;  // Controlled_Buffer controlled_buffer_56
  assign controlled_buffer_1_out = and_47_out ? 1'b1 : 1'bz;  // Controlled_Buffer controlled_buffer_57
  and and_48 (and_48_out, and_56_out, decoder_1_out2);
  assign {controlled_buffer_2_out_6, controlled_buffer_2_out_5, RAM_LD__o, controlled_buffer_2_out_4, controlled_buffer_2_out_3, controlled_buffer_2_out_2, controlled_buffer_2_out} = and_48_out ? 30'h320025 : 30'bz;  // Controlled_Buffer controlled_buffer_58
  assign controlled_buffer_1_out = and_48_out ? 1'b1 : 1'bz;  // Controlled_Buffer controlled_buffer_59
  and and_49 (and_49_out, and_52_out, decoder_1_out2);
  assign {controlled_buffer_2_out_6, controlled_buffer_2_out_5, RAM_LD__o, controlled_buffer_2_out_4, controlled_buffer_2_out_3, controlled_buffer_2_out_2, controlled_buffer_2_out} = and_49_out ? 30'h320025 : 30'bz;  // Controlled_Buffer controlled_buffer_60
  assign controlled_buffer_1_out = and_49_out ? 1'b1 : 1'bz;  // Controlled_Buffer controlled_buffer_61
  and and_50 (and_50_out, and_53_out, decoder_1_out2);
  assign {controlled_buffer_2_out_6, controlled_buffer_2_out_5, RAM_LD__o, controlled_buffer_2_out_4, controlled_buffer_2_out_3, controlled_buffer_2_out_2, controlled_buffer_2_out} = and_50_out ? 30'h320025 : 30'bz;  // Controlled_Buffer controlled_buffer_62
  assign controlled_buffer_1_out = and_50_out ? 1'b1 : 1'bz;  // Controlled_Buffer controlled_buffer_63
  Register #(.width(1)) register_1 (
    .D(comparator_1_gt), .en(controlled_buffer_2_out_4[11]), .clk(not_1_out), .Q(FLAG_____o), .clr(RESET__i));
  Counter #(.max('hffff), .width(16)) counter_2 (
    .load(controlled_buffer_2_out_4[16]), .D(ALU_Bus__o), .count(controlled_buffer_2_out_4[17]), .Q(IP__o),
    .up(1'b1), .clk(not_1_out), .clr(RESET__i));  // open: carry
  Register #(.width(1)) register_2 (
    .D(comparator_1_eq), .en(controlled_buffer_2_out_4[12]), .clk(not_1_out), .Q(FLAG_____o_2), .clr(RESET__i));
  Register #(.width(1)) register_3 (
    .D(comparator_1_lt), .en(controlled_buffer_2_out_4[13]), .clk(not_1_out), .Q(FLAG_____o_3), .clr(RESET__i));
  Register #(.width(1)) register_4 (
    .D(nor_1_out), .en(controlled_buffer_2_out_4[14]), .clk(not_1_out), .Q(FLAG__z__o), .clr(RESET__i));
  Multiplexer #(.enable("false"), .select(3), .width(16)) multiplexer_6 (
    .in0(R0__o), .in1(R1__o), .in2(R2__o), .in3(R3__o), .in4(IP__o), .in5(multiplexer_2_out),
    .in6(multiplexer_3_out), .out(RAM_INPUT__o), .sel(controlled_buffer_2_out_4[20:18]));  // open: in7
  Register #(.width(1)) register_5 (
    .D(controlled_buffer_35_out), .en(controlled_buffer_2_out_4[15]), .clk(not_1_out), .Q(FLAG__c__o),
    .clr(RESET__i));
  assign D_Bus__i = controlled_buffer_2_out_4[10] ? ALU_Bus__o : 16'bz;  // Controlled_Buffer controlled_buffer_64
  Register #(.trigger("falling"), .width(16)) register_6 (
    .D(D_Bus__i), .en(decoder_1_out0), .clk(not_1_out), .Q(IR__o), .clr(RESET__i));
  and and_51 (and_51_out, ~multiplexer_7_out_3[9], ~multiplexer_7_out_3[10], ~multiplexer_7_out_3[11], ~multiplexer_7_out_3[12], ~multiplexer_7_out_3[13], ~multiplexer_7_out_3[14], ~multiplexer_7_out_3[15]);  // AND_Gate
  and and_52 (and_52_out, ~multiplexer_7_out_2[9], multiplexer_7_out_3[8], ~multiplexer_7_out_3[9], multiplexer_7_out_3[10], ~multiplexer_7_out_3[11], ~multiplexer_7_out_3[12], ~multiplexer_7_out_3[13], ~multiplexer_7_out_3[14], ~multiplexer_7_out_3[15]);  // AND_Gate
  and and_53 (and_53_out, multiplexer_7_out_2[9], multiplexer_7_out_3[8], ~multiplexer_7_out_3[9], multiplexer_7_out_3[10], ~multiplexer_7_out_3[11], ~multiplexer_7_out_3[12], ~multiplexer_7_out_3[13], ~multiplexer_7_out_3[14], ~multiplexer_7_out_3[15]);  // AND_Gate
  and and_54 (and_54_out, multiplexer_7_out_3[8], multiplexer_7_out_3[9], ~multiplexer_7_out_3[10], ~multiplexer_7_out_3[11], ~multiplexer_7_out_3[12], ~multiplexer_7_out_3[13], ~multiplexer_7_out_3[14], ~multiplexer_7_out_3[15]);  // AND_Gate
  and and_55 (and_55_out, ~multiplexer_7_out_3[8], multiplexer_7_out_3[9], ~multiplexer_7_out_3[10], ~multiplexer_7_out_3[11], ~multiplexer_7_out_3[12], ~multiplexer_7_out_3[13], ~multiplexer_7_out_3[14], ~multiplexer_7_out_3[15]);  // AND_Gate
  and and_56 (and_56_out, ~multiplexer_7_out_3[8], ~multiplexer_7_out_3[9], multiplexer_7_out_3[10], ~multiplexer_7_out_3[11], ~multiplexer_7_out_3[12], ~multiplexer_7_out_3[13], ~multiplexer_7_out_3[14], ~multiplexer_7_out_3[15]);  // AND_Gate
  and and_57 (and_57_out, multiplexer_7_out_3[8], multiplexer_7_out_3[9], multiplexer_7_out_3[10], ~multiplexer_7_out_3[11], ~multiplexer_7_out_3[12], ~multiplexer_7_out_3[13], ~multiplexer_7_out_3[14], ~multiplexer_7_out_3[15]);  // AND_Gate
  and and_58 (and_58_out, multiplexer_7_out_3[15], ~multiplexer_7_out_3[14], multiplexer_7_out_3[13], ~multiplexer_7_out_3[12], multiplexer_7_out_3[11], ~multiplexer_7_out_3[10], multiplexer_7_out_3[9], ~multiplexer_7_out_3[8], multiplexer_7_out_2[9], ~multiplexer_7_out_2[8], multiplexer_7_out_2[7], ~multiplexer_7_out_2[6], decoder_3_out0[1], ~decoder_3_out0[0], multiplexer_7_out[1], ~multiplexer_7_out[0]);  // AND_Gate
  Multiplexer #(.enable("false"), .width(16)) multiplexer_7 (
    .in0(IR__o), .in1(16'haaaa),
    .out({multiplexer_7_out_3, multiplexer_7_out_2[9:6], decoder_3_out0[1:0], multiplexer_7_out}),
    .sel(RESET__i));

  assign D_Bus__o = D_Bus__i;
endmodule
